// Logisim project CU_ALU_update_v1_5.circ as structural Verilog: 2 circuits, main circuit main
module main (
);

  ALU alu_1 ();  // open: I1B1, I2B1, I3B1, I2B2, I3B2, I4B2, I4B1, I1B2, E, out2, out3, out4, out1, Add, Sub, Relay, SL, SR, S5, S6, S7, Carry
  RAM ram_1 ();  // open: addr, data, sel, clk, ld, clr
  RAM ram_2 ();  // open: addr, data, sel, clk, ld, clr
endmodule

module ALU (
  input  I1B1,
  input  I2B1,
  input  I3B1,
  input  I4B1,
  input  I1B2,
  input  I2B2,
  input  I3B2,
  input  I4B2,
  input  E,
  input  Add,
  input  Sub,
  input  Relay,
  input  SL,
  input  SR,
  input  S5,
  input  S6,
  input  S7,
  output Carry,
  output out1,
  output out2,
  output out3,
  output out4
);

  wire [1:0] undriven;
  wire [2:0] priority_encoder_1_out;
  wire [3:0] main_1_c0, main_1_c4, main_2_out, main_3_a4, n4_bit_adder_1_output_4;

  _4_BIT_ADDER u_4_bit_adder_1 (
    .A_4({I4B1, I3B1, I2B1, I1B1}), .B_4({I4B2, I3B2, I2B2, I1B2}), .OVER_FLOW(Carry),
    .OUTPUT_4(n4_bit_adder_1_output_4));  // open: in_1
  multiplier_main main_1 (
    .A0(I1B1), .A1(I2B1), .A2(I3B1), .A3(I4B1), .B3(I4B2), .B2(I3B2), .B1(I2B2), .B0(I1B2),
    .C7(main_1_c4[3]), .C6(main_1_c4[2]), .C5(main_1_c4[1]), .C4(main_1_c4[0]), .C3(main_1_c0[3]),
    .C2(main_1_c0[2]), .C1(main_1_c0[1]), .C0(main_1_c0[0]));  // open: in_12, in_10, in_1, in_6
  FULL_SUB__1__main main_2 (
    .A({I4B1, I3B1, I2B1, I1B1}), .B({I4B2, I3B2, I2B2, I1B2}), .carryout(Carry), .out(main_2_out));  // open: Cin
  SHIFT_main main_3 (
    .I4(I4B1), .I3(I3B1), .I2(I2B1), .I1(I1B1), .Select_bits(undriven), .A4(main_3_a4[0]), .A3(main_3_a4[1]),
    .A2(main_3_a4[2]), .A1(main_3_a4[3]));  // open: Shift_Right, Shift_Left
  Decoder #(.select(2)) decoder_1 (.out1(SR), .out2(SL), .out3(Relay), .sel(undriven));  // open: out0, en
  Multiplexer #(.select(3), .width(4)) multiplexer_1 (
    .in0(n4_bit_adder_1_output_4), .in1(main_2_out), .in3(main_3_a4), .in4(main_3_a4),
    .out({out4, out3, out2, out1}), .sel(priority_encoder_1_out), .en(E));  // open: in2, in5, in6, in7
  Priority_Encoder #(.disabled(0)) priority_encoder_1 (
    .in0(Add), .in1(Sub), .in2(Relay), .in3(SL), .in4(SR), .in5(S5), .in6(S6), .in7(S7),
    .out(priority_encoder_1_out));  // open: en_in
endmodule
