// Logisim project CU_v1_5.circ as structural Verilog: 5 circuits, main circuit main
module main (
  input  DME,
  input  PCE,
  input  DMRW,
  input  PCIE,
  input  TRE,
  input  IME,
  input  TRRW,
  input  IMRW,
  input  L3E,
  input  L5E,
  input  ARE,
  input  ACCE,
  input  ACCRW,
  input  CRRW,
  input  L4E,
  input  CRW,
  input  ROE,
  input  RORW,
  input  L1E,
  input  ADDE,
  input  SUBE,
  input  SHL,
  input  SLE,
  input  SRE,
  input  MULE,
  input  ALUE,
  input  ALUC,
  input  CLK,
  input  HIE,
  input  HIRW,
  input  LOE,
  input  LORW,
  output [3:0] out_33,
  output [3:0] out_34,
  output [9:0] out_35,
  output [3:0] out_36,
  output [3:0] out_37,
  output [3:0] out_38,
  output [3:0] out_39
);

  wire ADD, Carry_data, EXIT, LLS, LOAD, LOAD_ADDRESS, Load_CARRY, LOAD_HI, LOAD_LO, LRS, MOVE, MUL, STORE,
       SUB;
  wire [1:0] and_2_out, and_2_out_2, L1, L1A_out, L1B_out, L3, not_1_out, TRS;
  wire [3:0] adder_1_out, alu_1_hi, alu_1_lo, and_1_out;

  Pull_Resistor pull_resistor_1 (.node(out_37));
  Adder #(.width(4)) adder_1 (.a(out_33), .b(4'b0001), .out(adder_1_out));  // open: cin, cout
  assign and_1_out = adder_1_out & {4{PCIE}};  // AND_Gate and_1, 4 bits wide
  TempReg tempreg_1 (.CLK(CLK), .DO(out_36), .RS(TRS), .E(TRE), .DI(out_36), .RW(TRRW));
  Registor ACC (.E(ACCE), .CLK(CLK), .DO(out_37), .RW(ACCRW), .DI(out_37));
  Register #(.width(4)) register_1 (.D(and_1_out), .en(PCE), .Q(out_33), .clk(CLK), .clr(1'b0));
  assign out_37 = out_36 & {4{L4E}};  // AND_Gate L4, 4 bits wide
  Decoder #(.select(4)) decoder_1 (
    .out0(LOAD_LO), .out1(LOAD), .out2(STORE), .out3(ADD), .out4(SUB), .out5(LRS), .out6(LLS), .out7(MUL),
    .out8(LOAD_HI), .out9(LOAD_ADDRESS), .out10(MOVE), .out11(Load_CARRY), .out15(EXIT), .sel(out_35[9:6]));  // open: out12, out13, out14, en
  Pull_Resistor pull_resistor_2 (.node(out_36));
  Registor_1bit Carry (.E(CRRW), .CLK(CLK), .RW(CRW), .Data(Carry_data));
  ALU alu_1 (
    .Carry(Carry_data), .E(ALUE), .Add(ADDE), .Sub(SUBE), .SLO(SHL), .SL(SLE), .SR(SRE), .Mul(MULE),
    .Clear(ALUC), .Out(out_39), .LO(alu_1_lo), .HI(alu_1_hi), .In1(out_36), .In2(out_37));  // open: S6
  assign out_36 = {4{L5E}} & out_39;  // AND_Gate L5, 4 bits wide
  Registor HI (.E(HIE), .CLK(CLK), .DO(alu_1_hi), .RW(HIRW));  // open: DI
  assign L3 = out_35[5:4] & {2{L3E}};  // AND_Gate L3, 2 bits wide
  Registor OR (.E(ROE), .CLK(CLK), .DO(out_39), .RW(RORW), .DI(out_39));
  Registor LO (.E(LOE), .CLK(CLK), .DO(alu_1_lo), .RW(LORW));  // open: DI
  RAM #(.addrWidth(4), .dataWidth(4)) ram_1 (
    .addr(out_34), .data(out_36), .sel(DME), .clk(CLK), .ld(DMRW));  // open: clr
  RAM #(.addrWidth(4), .dataWidth(10)) ram_2 (
    .addr(out_33), .data({out_35[9:4], out_34}), .sel(IME), .clk(CLK), .ld(IMRW));  // open: clr
  Pull_Resistor pull_resistor_3 (.node(out_39));
  assign TRS = L1 | L3;  // OR_Gate or_2, 2 bits wide
  Pull_Resistor pull_resistor_4 (.node({out_35[9:4], out_34}));
  Pull_Resistor pull_resistor_5 (.node(out_34));
  assign not_1_out = ~{2{L1E}};  // NOT_Gate not_1, 2 bits wide
  assign L1A_out = {2{L1E}} & and_2_out;  // AND_Gate L1A, 2 bits wide
  assign L1 = L1A_out | L1B_out;  // OR_Gate or_3, 2 bits wide
  assign {and_2_out, and_2_out_2} = {4{ARE}} & out_34;  // AND_Gate and_2, 4 bits wide
  assign L1B_out = and_2_out_2 & not_1_out;  // AND_Gate L1B, 2 bits wide

  assign out_35[3:0] = out_34;
  assign out_38 = out_36;

  // Other names for the same wires on the sheet: IMUX[3:0] = out_35[9:6]

  // Notes on the sheet:
  //   L4 drives only 1 and floats otherwise
  //   L5 drives only 1 and floats otherwise
endmodule

module ALU (
  input  [3:0] In1,
  input  [3:0] In2,
  input  E,
  input  Add,
  input  Sub,
  input  SLO,
  input  SL,
  input  SR,
  input  Mul,
  input  S6,
  input  Clear,
  output Carry,
  output [3:0] Out,
  output [3:0] HI,
  output [3:0] LO
);

  wire [1:0] undriven;
  wire [2:0] priority_encoder_1_out;
  wire [3:0] add_output_4, Shift_a4, Sub_out;

  _4_BIT_ADDER u_add (.A_4(In1), .B_4(In2), .OVER_FLOW(Carry), .in_1(1'b0), .OUTPUT_4(add_output_4));
  multiplier_main u_Mul (
    .A0(In1[0]), .A1(In1[1]), .A2(In1[2]), .A3(In1[3]), .B3(In2[3]), .B2(In2[2]), .B1(In2[1]), .B0(In2[0]),
    .C7(HI[3]), .C6(HI[2]), .C5(HI[1]), .C4(HI[0]), .C3(LO[3]), .C2(LO[2]), .C1(LO[1]), .C0(LO[0]));  // open: in_12, in_10, in_1, in_6
  Pull_Resistor pull_resistor_1 (.node(In1));
  Pull_Resistor pull_resistor_2 (.node(In2));
  SHIFT_main Shift (
    .I4(In1[3]), .I3(In1[2]), .I2(In1[1]), .I1(In1[0]), .Select_bits(undriven), .A4(Shift_a4[0]),
    .A3(Shift_a4[1]), .A2(Shift_a4[2]), .A1(Shift_a4[3]));  // open: Shift_Right, Shift_Left
  FULL_SUB__1__main u_Sub (.A(In1), .B(In2), .carryout(Carry), .out(Sub_out));  // open: Cin
  Decoder #(.select(2)) decoder_1 (.out1(SR), .out2(SL), .out3(SLO), .sel(undriven));  // open: out0, en
  Multiplexer #(.select(3), .width(4)) multiplexer_1 (
    .in0(add_output_4), .in1(Sub_out), .in3(Shift_a4), .in4(Shift_a4), .in5(LO), .in7(4'b0000), .out(Out),
    .sel(priority_encoder_1_out), .en(E));  // open: in2, in6
  Priority_Encoder #(.disabled(0)) priority_encoder_1 (
    .in0(Add), .in1(Sub), .in2(SLO), .in3(SL), .in4(SR), .in5(Mul), .in6(S6), .in7(Clear),
    .out(priority_encoder_1_out));  // open: en_in
endmodule

// RegistorBank
module TempReg (
  input  E,
  input  [1:0] RS,
  input  [3:0] DI,
  input  CLK,
  input  RW,
  output [3:0] DO
);

  wire and_1_out, demultiplexer_1_out0, demultiplexer_1_out1, demultiplexer_1_out2, demultiplexer_1_out3,
       not_2_out;
  wire [3:0] and_2_out, multiplexer_1_out, not_1_out, register_1_q, register_2_q, register_3_q, register_4_q;

  Demultiplexer #(.select(2), .disabled(0)) demultiplexer_1 (
    .out0(demultiplexer_1_out0), .out1(demultiplexer_1_out1), .out2(demultiplexer_1_out2),
    .out3(demultiplexer_1_out3), .in(1'b1), .sel(RS), .en(E));
  and and_1 (and_1_out, CLK, not_2_out);
  Register #(.width(4)) register_1 (
    .D(and_2_out), .en(demultiplexer_1_out0), .Q(register_1_q), .clk(and_1_out), .clr(1'b0));
  Register #(.width(4)) register_2 (
    .D(and_2_out), .en(demultiplexer_1_out1), .Q(register_2_q), .clk(and_1_out), .clr(1'b0));
  Register #(.width(4)) register_3 (
    .D(and_2_out), .en(demultiplexer_1_out2), .Q(register_3_q), .clk(and_1_out), .clr(1'b0));
  Register #(.width(4)) register_4 (
    .D(and_2_out), .en(demultiplexer_1_out3), .Q(register_4_q), .clk(and_1_out), .clr(1'b0));
  assign and_2_out = DI & not_1_out;  // AND_Gate and_2, 4 bits wide
  assign not_1_out = ~{4{RW}};  // NOT_Gate not_1, 4 bits wide
  not not_2 (not_2_out, RW);
  Multiplexer #(.select(2), .width(4), .disabled(0)) multiplexer_1 (
    .in0(register_1_q), .in1(register_2_q), .in2(register_3_q), .in3(register_4_q), .out(multiplexer_1_out),
    .sel(RS), .en(E));
  assign DO = multiplexer_1_out & {4{RW}};  // AND_Gate and_3, 4 bits wide

  // Notes on the sheet:
  //   DO: pull=down
  //   DI: pull=down
  //   and_3 drives only 1 and floats otherwise
endmodule

module Registor (
  input  E,
  input  [3:0] DI,
  input  CLK,
  input  RW,
  output [3:0] DO
);

  wire and_1_out, not_2_out;
  wire [3:0] and_2_out, not_1_out, Reg_q;

  and and_1 (and_1_out, CLK, not_2_out);
  assign and_2_out = DI & not_1_out;  // AND_Gate and_2, 4 bits wide
  Register #(.width(4)) Reg (.D(and_2_out), .en(E), .Q(Reg_q), .clk(and_1_out));  // open: clr
  assign not_1_out = ~{4{RW}};  // NOT_Gate not_1, 4 bits wide
  not not_2 (not_2_out, RW);
  assign DO = Reg_q & {4{RW}};  // AND_Gate and_3, 4 bits wide

  // Notes on the sheet:
  //   CLK: pull=down
  //   and_3 drives only 1 and floats otherwise
endmodule

module Registor_1bit (
  input  E,
  input  RW,
  input  CLK,
  output Data
);

  wire Reg_q, undriven;

  Register #(.width(1)) Reg (.D(undriven), .en(E), .Q(Reg_q), .clk(CLK));  // open: clr
  Multiplexer multiplexer_1 (.in0(undriven), .in1(Reg_q), .out(Data), .en(RW));  // open: sel
endmodule
