// Logisim project ALU_MUX_mod.circ as structural Verilog
module _1_BIT_ADDER (
  input  A,
  input  B,
  input  CARRY_IN,
  output OUTPUT,
  output CARRY_OUT
);

  wire and_1_out, and_2_out, and_3_out, and_4_out, and_5_out, and_6_out, and_7_out, not_1_out, not_2_out,
       not_3_out;

  not not_1 (not_1_out, A);
  not not_2 (not_2_out, B);
  not not_3 (not_3_out, CARRY_IN);
  and and_1 (and_1_out, not_1_out, B, CARRY_IN);
  and and_2 (and_2_out, A, B, not_3_out);
  and and_3 (and_3_out, A, not_2_out, CARRY_IN);
  or or_1 (CARRY_OUT, and_1_out, and_3_out, and_2_out, and_4_out);
  and and_4 (and_4_out, A, B, CARRY_IN);
  and and_5 (and_5_out, not_1_out, B, not_3_out);
  and and_6 (and_6_out, not_1_out, not_2_out, CARRY_IN);
  or or_2 (OUTPUT, and_4_out, and_6_out, and_5_out, and_7_out);
  and and_7 (and_7_out, A, not_2_out, not_3_out);
endmodule

module _4_BIT_ADDER (
  input  in_1,
  input  [3:0] A_4,
  input  [3:0] B_4,
  output [3:0] OUTPUT_4,
  output OVER_FLOW
);

  wire n1_bit_adder_1_carry_out, n1_bit_adder_2_carry_out, n1_bit_adder_3_carry_out;

  _1_BIT_ADDER u_1_bit_adder_1 (
    .A(A_4[0]), .B(B_4[0]), .CARRY_IN(in_1), .OUTPUT(OUTPUT_4[0]), .CARRY_OUT(n1_bit_adder_1_carry_out));
  _1_BIT_ADDER u_1_bit_adder_2 (
    .A(A_4[1]), .B(B_4[1]), .CARRY_IN(n1_bit_adder_1_carry_out), .OUTPUT(OUTPUT_4[1]),
    .CARRY_OUT(n1_bit_adder_2_carry_out));
  _1_BIT_ADDER u_1_bit_adder_3 (
    .A(A_4[2]), .B(B_4[2]), .CARRY_IN(n1_bit_adder_2_carry_out), .OUTPUT(OUTPUT_4[2]),
    .CARRY_OUT(n1_bit_adder_3_carry_out));
  _1_BIT_ADDER u_1_bit_adder_4 (
    .A(A_4[3]), .B(B_4[3]), .CARRY_IN(n1_bit_adder_3_carry_out), .OUTPUT(OUTPUT_4[3]), .CARRY_OUT(OVER_FLOW));
endmodule

module MUX_ALU (
  input  in_1,
  input  [3:0] IN_A,
  input  [3:0] IN_B,
  input  in_4,
  input  [2:0] OP_CODE,
  output [3:0] OUT
);

  wire [3:0] divider_1_out, multiplier_1_out, n4_bit_adder_1_output_4, subtractor_1_out;

  _4_BIT_ADDER u_4_bit_adder_1 (
    .A_4(IN_A), .B_4(IN_B), .in_1(in_1), .OUTPUT_4(n4_bit_adder_1_output_4));  // open: OVER_FLOW
  Subtractor #(.width(4)) subtractor_1 (.a(IN_A), .b(IN_B), .out(subtractor_1_out));  // open: bin, bout
  Multiplier #(.width(4)) multiplier_1 (.a(IN_A), .b(IN_B), .out(multiplier_1_out));  // open: cin, cout
  Divider #(.width(4)) divider_1 (.a(IN_A), .b(IN_B), .out(divider_1_out));  // open: upper, rem
  Multiplexer #(.select(3), .width(4)) multiplexer_1 (
    .in0(n4_bit_adder_1_output_4), .in1(subtractor_1_out), .in2(multiplier_1_out), .in3(divider_1_out),
    .out(OUT), .sel(OP_CODE), .en(in_4));  // open: in4, in5, in6, in7
endmodule
