// Logisim project CU_v2_1.circ as structural Verilog: 5 circuits, main circuit main
module main (
  input  PCRST,
  output [3:0] out_2,
  output [3:0] out_3,
  output [9:0] out_4,
  output [3:0] out_5,
  output [1:0] out_6,
  output [3:0] out_7,
  output [3:0] out_8,
  output [3:0] out_9
);

  wire ACCE, ACCRW, ADD, ADDE, ALUC, ALUE, and_2_out, and_3_out, and_4_out, and_5_out, and_6_out, and_7_out,
       and_8_out, and_9_out, and_10_out, and_12_out, and_13_out, and_14_out, and_15_out, and_16_out,
       and_17_out, and_18_out, and_19_out, buffer_38_out, buffer_57_out, CLK, CRE, CRRW, DME, DMRW, EXIT,
       HIE, HIRW, IME, INSEND, L1E, L2E, L3E, L4E, L5E, L6E, L7E, L8E, LLS, LOAD_ADDRESS, LOAD_CARRY,
       LOAD_HI, LOAD_IMMEDIATE, LOAD_LO, LOE, LORW, LRS, MOVE, MUL, MULE, nor_1_out, not_4_out, not_6_out,
       not_7_out, not_9_out, not_11_out, not_12_out, not_16_out, not_17_out, not_19_out, not_21_out,
       not_22_out, not_23_out, not_24_out, not_26_out, not_27_out, not_29_out, not_37_out, PCE, ROE, RORW,
       RSTINS, s_r_ff_1_q, shift_register_1_q0, shift_register_1_q1, shift_register_1_q2,
       shift_register_2_q0, shift_register_2_q1, shift_register_2_q2, shift_register_3_q0,
       shift_register_3_q1, shift_register_3_q2, shift_register_4_q0, shift_register_4_q1,
       shift_register_4_q2, shift_register_5_q0, shift_register_5_q1, shift_register_5_q2,
       shift_register_5_q3, shift_register_5_q4, shift_register_6_q0, shift_register_6_q1,
       shift_register_6_q2, shift_register_7_q1, shift_register_7_q2, shift_register_7_q3,
       shift_register_7_q4, shift_register_7_q5, shift_register_8_q0, shift_register_8_q1,
       shift_register_8_q2, shift_register_8_q3, shift_register_8_q4, shift_register_8_q5,
       shift_register_8_q6, shift_register_9_q0, shift_register_9_q1, shift_register_9_q2,
       shift_register_9_q4, shift_register_9_q5, shift_register_9_q6, shift_register_9_q7,
       shift_register_10_q0, shift_register_10_q1, shift_register_10_q2, shift_register_11_q0,
       shift_register_11_q1, shift_register_11_q2, SHL, SLE, SRE, STORE, SUB, SUBE, TRE, TRRW;
  wire [1:0] L1, L1A_out, L1B_out, L2_out, L2_out_2, L3, not_30_out;
  wire [3:0] adder_1_out, alu_1_carry, alu_1_hi, alu_1_lo, and_1_out;

  Pull_Resistor pull_resistor_1 (.node(out_7));
  assign out_6 = L1 | L3;  // OR_Gate or_1, 2 bits wide
  buf buffer_1 (DME, and_5_out);
  buf buffer_2 (CRRW, and_2_out);
  buf buffer_3 (LORW, and_3_out);
  buf buffer_4 (L2E, and_6_out);
  buf buffer_5 (TRRW, and_6_out);
  Adder #(.width(4)) adder_1 (.a(out_2), .b(4'b0001), .out(adder_1_out));  // open: cin, cout
  assign and_1_out = adder_1_out & {4{PCE}};  // AND_Gate and_1, 4 bits wide
  TempReg tempreg_1 (.CLK(CLK), .DO(out_5), .RS(out_6), .E(TRE), .DI(out_5), .RW(TRRW));
  Registor ACC (.E(ACCE), .CLK(CLK), .DO(out_7), .RW(ACCRW), .DI(out_7));
  assign out_7 = out_5 & {4{L4E}};  // AND_Gate L4, 4 bits wide
  Decoder #(.select(4)) decoder_1 (
    .out0(LOAD_LO), .out1(LOAD_IMMEDIATE), .out2(STORE), .out3(ADD), .out4(SUB), .out5(LRS), .out6(LLS),
    .out7(MUL), .out8(LOAD_HI), .out9(LOAD_ADDRESS), .out10(MOVE), .out11(LOAD_CARRY), .out15(EXIT),
    .sel(out_4[9:6]));  // open: out12, out13, out14, en
  buf buffer_6 (ADDE, ADD);
  buf buffer_7 (SUBE, SUB);
  buf buffer_8 (MULE, MUL);
  Shift_Register #(.length(3)) shift_register_1 (
    .shift(LOAD_ADDRESS), .in(1'b1), .clk(CLK), .clr(RSTINS), .q0(shift_register_1_q0),
    .q1(shift_register_1_q1), .q2(shift_register_1_q2));  // open: out, load, d0, d1, d2
  buf buffer_9 (DME, and_4_out);
  buf buffer_10 (DMRW, and_4_out);
  Shift_Register #(.length(3)) shift_register_2 (
    .shift(STORE), .in(1'b1), .clk(CLK), .clr(RSTINS), .q0(shift_register_2_q0), .q1(shift_register_2_q1),
    .q2(shift_register_2_q2));  // open: out, load, d0, d1, d2
  not not_1 (DMRW, and_5_out);
  Shift_Register #(.length(3)) shift_register_3 (
    .shift(LOAD_CARRY), .in(1'b1), .clk(CLK), .clr(RSTINS), .q0(shift_register_3_q0),
    .q1(shift_register_3_q1), .q2(shift_register_3_q2));  // open: out, load, d0, d1, d2
  and and_2 (and_2_out, shift_register_3_q0, not_7_out);
  buf buffer_11 (CRE, and_2_out);
  buf buffer_12 (L3E, and_2_out);
  Shift_Register #(.length(3)) shift_register_4 (
    .shift(LOAD_LO), .in(1'b1), .clk(CLK), .clr(RSTINS), .q0(shift_register_4_q0), .q1(shift_register_4_q1),
    .q2(shift_register_4_q2));  // open: out, load, d0, d1, d2
  and and_3 (and_3_out, shift_register_4_q0, not_9_out);
  buf buffer_13 (LOE, and_3_out);
  buf buffer_14 (L3E, and_3_out);
  Shift_Register #(.length(5)) shift_register_5 (
    .shift(MOVE), .in(1'b1), .clk(CLK), .clr(RSTINS), .q0(shift_register_5_q0), .q1(shift_register_5_q1),
    .q2(shift_register_5_q2), .q3(shift_register_5_q3), .q4(shift_register_5_q4));  // open: out, load, d0, d1, d2, d3, d4
  buf buffer_15 (ACCE, and_6_out);
  not not_2 (L1E, and_6_out);
  buf buffer_16 (L4E, and_6_out);
  not not_3 (ACCRW, and_6_out);
  buf buffer_17 (TRE, and_6_out);
  Register #(.width(4)) register_1 (.D(and_1_out), .en(PCE), .Q(out_2), .clk(CLK), .clr(PCRST));
  assign out_5 = {4{L8E}} & out_7;  // AND_Gate L8, 4 bits wide
  buf buffer_18 (INSEND, shift_register_1_q2);
  not not_4 (not_4_out, shift_register_1_q1);
  and and_4 (and_4_out, shift_register_1_q0, not_4_out);
  buf buffer_19 (TRE, and_4_out);
  buf buffer_20 (L3E, and_4_out);
  not not_5 (TRRW, and_4_out);
  buf buffer_21 (INSEND, shift_register_2_q2);
  not not_6 (not_6_out, shift_register_2_q1);
  and and_5 (and_5_out, shift_register_2_q0, not_6_out);
  buf buffer_22 (L3E, and_5_out);
  buf buffer_23 (TRE, and_5_out);
  buf buffer_24 (TRRW, and_5_out);
  buf buffer_25 (INSEND, shift_register_3_q2);
  not not_7 (not_7_out, shift_register_3_q1);
  buf buffer_26 (TRE, and_2_out);
  not not_8 (TRRW, and_2_out);
  buf buffer_27 (INSEND, shift_register_4_q2);
  not not_9 (not_9_out, shift_register_4_q1);
  not not_10 (TRRW, and_3_out);
  buf buffer_28 (TRE, and_3_out);
  not not_11 (not_11_out, shift_register_5_q3);
  not not_12 (not_12_out, shift_register_5_q1);
  and and_6 (and_6_out, shift_register_5_q0, not_12_out);
  and and_7 (and_7_out, shift_register_5_q2, not_11_out);
  buf buffer_29 (ACCE, and_7_out);
  Pull_Resistor pull_resistor_2 (.node(out_5));
  assign out_5 = {{3{alu_1_carry[3]}}, alu_1_carry[0]} & {4{L6E}};  // AND_Gate L6, 4 bits wide
  buf buffer_30 (ACCE, and_8_out);
  buf buffer_31 (ACCE, and_12_out);
  buf buffer_32 (CRRW, and_9_out);
  buf buffer_33 (INSEND, shift_register_5_q4);
  not not_13 (TRRW, and_7_out);
  buf buffer_34 (TRE, and_7_out);
  buf buffer_35 (L8E, and_7_out);
  buf buffer_36 (ACCRW, and_7_out);
  buf buffer_37 (L3E, and_7_out);
  assign out_5 = {4{L7E}} & out_3;  // AND_Gate L7, 4 bits wide
  ALU alu_1 (
    .Carry(alu_1_carry[0]), .E(ALUE), .Add(ADDE), .Sub(SUBE), .SLO(SHL), .SL(SLE), .SR(SRE), .Mul(MULE),
    .Clear(ALUC), .Out(out_9), .HI(alu_1_hi), .LO(alu_1_lo), .In1(out_5), .In2(out_7), .CLK(CLK));  // open: S6
  Pull_Resistor pull_resistor_3 (.node(PCE));
  Pull_Resistor pull_resistor_4 (.node(PCE));
  Pull_Resistor pull_resistor_5 (.node(INSEND));
  buf buffer_38 (buffer_38_out, MUL);
  buf buffer_39 (buffer_38_out, SUB);
  buf buffer_40 (buffer_38_out, ADD);
  not not_14 (L1E, and_8_out);
  buf buffer_41 (TRRW, and_8_out);
  buf buffer_42 (L2E, and_8_out);
  buf buffer_43 (ACCRW, and_12_out);
  buf buffer_44 (L2E, and_12_out);
  Shift_Register #(.length(3)) shift_register_6 (
    .shift(LOAD_CARRY), .in(1'b1), .clk(CLK), .clr(RSTINS), .q0(shift_register_6_q0),
    .q1(shift_register_6_q1), .q2(shift_register_6_q2));  // open: out, load, d0, d1, d2
  buf buffer_45 (L3E, and_9_out);
  buf buffer_46 (CRE, and_9_out);
  buf buffer_47 (TRE, and_10_out);
  not not_15 (L1E, and_10_out);
  buf buffer_48 (ALUE, and_10_out);
  buf buffer_49 (TRRW, and_10_out);
  buf buffer_50 (TRRW, and_13_out);
  assign out_5 = {4{L5E}} & out_9;  // AND_Gate L5, 4 bits wide
  Registor CARRY (
    .E(CRE), .CLK(CLK), .DO({{3{alu_1_carry[3]}}, alu_1_carry[0]}), .RW(CRRW),
    .DI({{3{alu_1_carry[3]}}, alu_1_carry[0]}));
  Registor HI (.E(HIE), .CLK(CLK), .DO(alu_1_hi), .RW(HIRW));  // open: DI
  S_R_Flip_Flop s_r_ff_1 (
    .S(INSEND), .clk(CLK), .R(shift_register_7_q4), .Q(s_r_ff_1_q), .en(not_21_out));  // open: Qn, preset, reset
  Shift_Register #(.length(6)) shift_register_7 (
    .shift(s_r_ff_1_q), .in(1'b1), .clk(CLK), .clr(shift_register_7_q5), .q0(RSTINS),
    .q1(shift_register_7_q1), .q2(shift_register_7_q2), .q3(shift_register_7_q3), .q4(shift_register_7_q4),
    .q5(shift_register_7_q5));  // open: out, load, d0, d1, d2, d3, d4, d5
  Pull_Resistor pull_resistor_6 (.node(buffer_38_out));
  Shift_Register #(.length(7)) shift_register_8 (
    .shift(buffer_38_out), .in(1'b1), .clk(CLK), .clr(RSTINS), .q0(shift_register_8_q0),
    .q1(shift_register_8_q1), .q2(shift_register_8_q2), .q3(shift_register_8_q3), .q4(shift_register_8_q4),
    .q5(shift_register_8_q5), .q6(shift_register_8_q6));  // open: out, load, d0, d1, d2, d3, d4, d5, d6
  not not_16 (not_16_out, shift_register_8_q1);
  and and_8 (and_8_out, shift_register_8_q0, not_16_out);
  buf buffer_51 (TRE, and_8_out);
  buf buffer_52 (L4E, and_8_out);
  buf buffer_53 (TRE, and_12_out);
  buf buffer_54 (L1E, and_12_out);
  buf buffer_55 (INSEND, shift_register_6_q2);
  not not_17 (not_17_out, shift_register_6_q1);
  and and_9 (and_9_out, shift_register_6_q0, not_17_out);
  not not_18 (TRRW, and_9_out);
  buf buffer_56 (TRE, and_9_out);
  buf buffer_57 (buffer_57_out, LRS);
  Pull_Resistor pull_resistor_7 (.node(buffer_57_out));
  buf buffer_58 (buffer_57_out, LLS);
  Shift_Register shift_register_9 (
    .shift(buffer_57_out), .in(1'b1), .clk(CLK), .clr(RSTINS), .q0(shift_register_9_q0),
    .q1(shift_register_9_q1), .q2(shift_register_9_q2), .q4(shift_register_9_q4), .q5(shift_register_9_q5),
    .q6(shift_register_9_q6), .q7(shift_register_9_q7));  // open: out, load, d0, d1, d2, d3, q3, d4, d5, d6, d7
  not not_19 (not_19_out, shift_register_9_q1);
  buf buffer_59 (SHL, and_10_out);
  buf buffer_60 (L2E, and_10_out);
  and and_10 (and_10_out, shift_register_9_q0, not_19_out);
  not not_20 (RORW, and_13_out);
  buf buffer_61 (ROE, and_13_out);
  assign L3 = out_4[5:4] & {2{L3E}};  // AND_Gate L3, 2 bits wide
  Registor OR_2 (.E(ROE), .CLK(CLK), .DO(out_9), .RW(RORW), .DI(out_9));
  Registor LO (.E(LOE), .CLK(CLK), .DO(alu_1_lo), .RW(LORW));  // open: DI
  Pull_Resistor pull_resistor_8 (.node(ALUE));
  Pull_Resistor pull_resistor_9 (.node(ADDE));
  Pull_Resistor pull_resistor_10 (.node(SUBE));
  Pull_Resistor pull_resistor_11 (.node(SHL));
  Pull_Resistor pull_resistor_12 (.node(SLE));
  Pull_Resistor pull_resistor_13 (.node(SRE));
  Pull_Resistor pull_resistor_14 (.node(MULE));
  Pull_Resistor pull_resistor_15 (.node(ALUC));
  Pull_Resistor pull_resistor_16 (.node(HIE));
  Pull_Resistor pull_resistor_17 (.node(HIRW));
  Pull_Resistor pull_resistor_18 (.node(LOE));
  Pull_Resistor pull_resistor_19 (.node(LORW));
  not not_21 (not_21_out, shift_register_7_q5);
  not not_22 (not_22_out, shift_register_7_q2);
  and and_11 (PCE, shift_register_7_q1, not_22_out);
  buf buffer_62 (INSEND, shift_register_8_q6);
  not not_23 (not_23_out, shift_register_8_q5);
  not not_24 (not_24_out, shift_register_8_q3);
  not not_25 (ACCRW, and_8_out);
  and and_12 (and_12_out, shift_register_8_q2, not_24_out);
  buf buffer_63 (TRRW, and_12_out);
  buf buffer_64 (CRE, and_12_out);
  buf buffer_65 (HIRW, and_17_out);
  buf buffer_66 (HIE, and_17_out);
  not not_26 (not_26_out, shift_register_9_q4);
  not not_27 (not_27_out, shift_register_9_q6);
  and and_13 (and_13_out, shift_register_9_q2, not_26_out);
  and and_14 (and_14_out, and_13_out, LRS);
  and and_15 (and_15_out, and_13_out, LLS);
  buf buffer_67 (SLE, and_15_out);
  buf buffer_68 (SRE, and_14_out);
  RAM #(.addrWidth(4), .dataWidth(4)) ram_1 (.addr(out_3), .data(out_5), .sel(DME), .clk(CLK), .ld(DMRW));  // open: clr
  RAM #(.addrWidth(4), .dataWidth(10)) ram_2 (
    .addr(out_2), .data({out_4[9:4], out_3}), .sel(IME), .clk(CLK), .ld(IME));  // open: clr
  Pull_Resistor pull_resistor_20 (.node(out_9));
  Pull_Resistor pull_resistor_21 (.node(L1E));
  Pull_Resistor pull_resistor_22 (.node(L2E));
  Pull_Resistor pull_resistor_23 (.node(L3E));
  Pull_Resistor pull_resistor_24 (.node(L4E));
  Pull_Resistor pull_resistor_25 (.node(L5E));
  Pull_Resistor pull_resistor_26 (.node(L6E));
  Pull_Resistor pull_resistor_27 (.node(L7E));
  Pull_Resistor pull_resistor_28 (.node(L8E));
  Pull_Resistor pull_resistor_29 (.node(IME));
  Pull_Resistor pull_resistor_30 (.node(IME));
  Pull_Resistor pull_resistor_31 (.node(DMRW));
  Pull_Resistor pull_resistor_32 (.node(DME));
  nor nor_1 (nor_1_out, shift_register_7_q3, INSEND, IME);
  and and_16 (and_16_out, not_23_out, shift_register_8_q4);
  buf buffer_69 (L5E, and_16_out);
  buf buffer_70 (TRE, and_16_out);
  buf buffer_71 (L3E, and_16_out);
  not not_28 (CRRW, and_12_out);
  buf buffer_72 (ROE, and_12_out);
  Shift_Register #(.length(3)) shift_register_10 (
    .shift(LOAD_HI), .in(1'b1), .clk(CLK), .clr(RSTINS), .q0(shift_register_10_q0),
    .q1(shift_register_10_q1), .q2(shift_register_10_q2));  // open: out, load, d0, d1, d2
  not not_29 (not_29_out, shift_register_10_q1);
  and and_17 (and_17_out, shift_register_10_q0, not_29_out);
  buf buffer_73 (L3E, and_17_out);
  buf buffer_74 (TRE, and_17_out);
  buf buffer_75 (INSEND, shift_register_9_q7);
  and and_18 (and_18_out, not_27_out, shift_register_9_q5);
  buf buffer_76 (L3E, and_18_out);
  buf buffer_77 (ALUE, and_13_out);
  buf buffer_78 (TRE, and_13_out);
  Pull_Resistor pull_resistor_33 (.node({out_4[9:4], out_3}));
  Pull_Resistor pull_resistor_34 (.node(out_3));
  assign not_30_out = ~{2{L1E}};  // NOT_Gate not_30, 2 bits wide
  assign L1A_out = {2{L1E}} & L2_out;  // AND_Gate L1A, 2 bits wide
  assign L1 = L1A_out | L1B_out;  // OR_Gate or_3, 2 bits wide
  Pull_Resistor pull_resistor_35 (.node(TRE));
  Pull_Resistor pull_resistor_36 (.node(TRRW));
  Pull_Resistor pull_resistor_37 (.node(CRRW));
  Pull_Resistor pull_resistor_38 (.node(CRE));
  Pull_Resistor pull_resistor_39 (.node(RORW));
  Pull_Resistor pull_resistor_40 (.node(ROE));
  Pull_Resistor pull_resistor_41 (.node(ACCRW));
  Pull_Resistor pull_resistor_42 (.node(ACCE));
  S_R_Flip_Flop s_r_ff_2 (
    .S(shift_register_7_q3), .clk(CLK), .R(INSEND), .Q(IME), .preset(nor_1_out), .en(1'b1));  // open: Qn, reset
  buf buffer_79 (RORW, and_16_out);
  buf buffer_80 (ROE, and_16_out);
  not not_31 (TRRW, and_16_out);
  not not_32 (RORW, and_12_out);
  buf buffer_81 (ALUE, and_12_out);
  buf buffer_82 (INSEND, shift_register_10_q2);
  not not_33 (TRRW, and_17_out);
  buf buffer_83 (L5E, and_18_out);
  buf buffer_84 (RORW, and_18_out);
  not not_34 (TRRW, and_18_out);
  buf buffer_85 (TRE, and_18_out);
  Clock u_CLK (.out(CLK));
  assign {L2_out, L2_out_2} = {4{L2E}} & out_3;  // AND_Gate L2, 4 bits wide
  assign L1B_out = L2_out_2 & not_30_out;  // AND_Gate L1B, 2 bits wide
  buf buffer_86 (LOE, and_12_out);
  buf buffer_87 (HIE, and_12_out);
  not not_35 (LORW, and_12_out);
  not not_36 (HIRW, and_12_out);
  Shift_Register #(.length(3)) shift_register_11 (
    .shift(LOAD_IMMEDIATE), .in(1'b1), .clk(CLK), .clr(RSTINS), .q0(shift_register_11_q0),
    .q1(shift_register_11_q1), .q2(shift_register_11_q2));  // open: out, load, d0, d1, d2
  buf buffer_88 (L7E, and_19_out);
  buf buffer_89 (L3E, and_19_out);
  buf buffer_90 (ROE, and_18_out);
  buf buffer_91 (INSEND, shift_register_11_q2);
  not not_37 (not_37_out, shift_register_11_q1);
  and and_19 (and_19_out, shift_register_11_q0, not_37_out);
  not not_38 (TRRW, and_19_out);
  buf buffer_92 (TRE, and_19_out);

  assign out_4[3:0] = out_3;
  assign out_8 = out_5;
  // also tied to GND on the sheet: alu_1_carry[3]

  // Other names for the same wires on the sheet: PCIE = PCE; IMRW = IME; IMUX[3:0] = out_4[9:6]; TRS[1:0] = out_6

  // Notes on the sheet:
  //   buffer_1 drives only 1 and floats otherwise
  //   buffer_2 drives only 1 and floats otherwise
  //   buffer_3 drives only 1 and floats otherwise
  //   buffer_4 drives only 1 and floats otherwise
  //   buffer_5 drives only 1 and floats otherwise
  //   L4 drives only 1 and floats otherwise
  //   buffer_6 drives only 1 and floats otherwise
  //   buffer_7 drives only 1 and floats otherwise
  //   buffer_8 drives only 1 and floats otherwise
  //   buffer_9 drives only 1 and floats otherwise
  //   buffer_10 drives only 1 and floats otherwise
  //   not_1 drives only 0 and floats otherwise
  //   buffer_11 drives only 1 and floats otherwise
  //   buffer_12 drives only 1 and floats otherwise
  //   buffer_13 drives only 1 and floats otherwise
  //   buffer_14 drives only 1 and floats otherwise
  //   buffer_15 drives only 1 and floats otherwise
  //   not_2 drives only 0 and floats otherwise
  //   buffer_16 drives only 1 and floats otherwise
  //   not_3 drives only 0 and floats otherwise
  //   buffer_17 drives only 1 and floats otherwise
  //   L8 drives only 1 and floats otherwise
  //   buffer_18 drives only 1 and floats otherwise
  //   buffer_19 drives only 1 and floats otherwise
  //   buffer_20 drives only 1 and floats otherwise
  //   not_5 drives only 0 and floats otherwise
  //   buffer_21 drives only 1 and floats otherwise
  //   buffer_22 drives only 1 and floats otherwise
  //   buffer_23 drives only 1 and floats otherwise
  //   buffer_24 drives only 1 and floats otherwise
  //   buffer_25 drives only 1 and floats otherwise
  //   buffer_26 drives only 1 and floats otherwise
  //   not_8 drives only 0 and floats otherwise
  //   buffer_27 drives only 1 and floats otherwise
  //   not_10 drives only 0 and floats otherwise
  //   buffer_28 drives only 1 and floats otherwise
  //   buffer_29 drives only 1 and floats otherwise
  //   L6 drives only 1 and floats otherwise
  //   buffer_30 drives only 1 and floats otherwise
  //   buffer_31 drives only 1 and floats otherwise
  //   buffer_32 drives only 1 and floats otherwise
  //   buffer_33 drives only 1 and floats otherwise
  //   not_13 drives only 0 and floats otherwise
  //   buffer_34 drives only 1 and floats otherwise
  //   buffer_35 drives only 1 and floats otherwise
  //   buffer_36 drives only 1 and floats otherwise
  //   buffer_37 drives only 1 and floats otherwise
  //   L7 drives only 1 and floats otherwise
  //   buffer_38 drives only 1 and floats otherwise
  //   buffer_39 drives only 1 and floats otherwise
  //   buffer_40 drives only 1 and floats otherwise
  //   not_14 drives only 0 and floats otherwise
  //   buffer_41 drives only 1 and floats otherwise
  //   buffer_42 drives only 1 and floats otherwise
  //   buffer_43 drives only 1 and floats otherwise
  //   buffer_44 drives only 1 and floats otherwise
  //   buffer_45 drives only 1 and floats otherwise
  //   buffer_46 drives only 1 and floats otherwise
  //   buffer_47 drives only 1 and floats otherwise
  //   not_15 drives only 0 and floats otherwise
  //   buffer_48 drives only 1 and floats otherwise
  //   buffer_49 drives only 1 and floats otherwise
  //   buffer_50 drives only 1 and floats otherwise
  //   L5 drives only 1 and floats otherwise
  //   buffer_51 drives only 1 and floats otherwise
  //   buffer_52 drives only 1 and floats otherwise
  //   buffer_53 drives only 1 and floats otherwise
  //   buffer_54 drives only 1 and floats otherwise
  //   buffer_55 drives only 1 and floats otherwise
  //   not_18 drives only 0 and floats otherwise
  //   buffer_56 drives only 1 and floats otherwise
  //   buffer_57 drives only 1 and floats otherwise
  //   buffer_58 drives only 1 and floats otherwise
  //   buffer_59 drives only 1 and floats otherwise
  //   buffer_60 drives only 1 and floats otherwise
  //   not_20 drives only 0 and floats otherwise
  //   buffer_61 drives only 1 and floats otherwise
  //   and_11 drives only 1 and floats otherwise
  //   buffer_62 drives only 1 and floats otherwise
  //   not_25 drives only 0 and floats otherwise
  //   buffer_63 drives only 1 and floats otherwise
  //   buffer_64 drives only 1 and floats otherwise
  //   buffer_65 drives only 1 and floats otherwise
  //   buffer_66 drives only 1 and floats otherwise
  //   buffer_67 drives only 1 and floats otherwise
  //   buffer_68 drives only 1 and floats otherwise
  //   buffer_69 drives only 1 and floats otherwise
  //   buffer_70 drives only 1 and floats otherwise
  //   buffer_71 drives only 1 and floats otherwise
  //   not_28 drives only 0 and floats otherwise
  //   buffer_72 drives only 1 and floats otherwise
  //   buffer_73 drives only 1 and floats otherwise
  //   buffer_74 drives only 1 and floats otherwise
  //   buffer_75 drives only 1 and floats otherwise
  //   buffer_76 drives only 1 and floats otherwise
  //   buffer_77 drives only 1 and floats otherwise
  //   buffer_78 drives only 1 and floats otherwise
  //   buffer_79 drives only 1 and floats otherwise
  //   buffer_80 drives only 1 and floats otherwise
  //   not_31 drives only 0 and floats otherwise
  //   not_32 drives only 0 and floats otherwise
  //   buffer_81 drives only 1 and floats otherwise
  //   buffer_82 drives only 1 and floats otherwise
  //   not_33 drives only 0 and floats otherwise
  //   buffer_83 drives only 1 and floats otherwise
  //   buffer_84 drives only 1 and floats otherwise
  //   not_34 drives only 0 and floats otherwise
  //   buffer_85 drives only 1 and floats otherwise
  //   buffer_86 drives only 1 and floats otherwise
  //   buffer_87 drives only 1 and floats otherwise
  //   not_35 drives only 0 and floats otherwise
  //   not_36 drives only 0 and floats otherwise
  //   buffer_88 drives only 1 and floats otherwise
  //   buffer_89 drives only 1 and floats otherwise
  //   buffer_90 drives only 1 and floats otherwise
  //   buffer_91 drives only 1 and floats otherwise
  //   not_38 drives only 0 and floats otherwise
  //   buffer_92 drives only 1 and floats otherwise
endmodule

module ALU (
  input  [3:0] In1,
  input  [3:0] In2,
  input  E,
  input  Add,
  input  Sub,
  input  SLO,
  input  SL,
  input  SR,
  input  Mul,
  input  S6,
  input  Clear,
  input  CLK,
  output Carry,
  output [3:0] Out,
  output [3:0] LO,
  output [3:0] HI
);

  wire [1:0] priority_encoder_1_p3;
  wire [2:0] priority_encoder_2_out;
  wire [3:0] add_output_4, Mul_c3, Mul_c7, Shift_a1, Sub_out;

  _4_BIT_ADDER u_add (.A_4(In1), .B_4(In2), .OVER_FLOW(Carry), .in_1(1'b0), .OUTPUT_4(add_output_4));
  Multiplier #(.width(4)) multiplier_1 (.a(In1), .b(In2), .out(LO), .cout(HI));  // open: cin
  multiplier_main u_Mul (
    .A0(In1[0]), .A1(In1[1]), .A2(In1[2]), .A3(In1[3]), .B3(In2[3]), .B2(In2[2]), .B1(In2[1]), .B0(In2[0]),
    .C7(Mul_c7[0]), .C6(Mul_c7[1]), .C5(Mul_c7[2]), .C4(Mul_c7[3]), .C3(Mul_c3[0]), .C2(Mul_c3[1]),
    .C1(Mul_c3[2]), .C0(Mul_c3[3]));  // open: in_12, in_10, in_1, in_6
  Pull_Resistor pull_resistor_1 (.node(In1));
  Pull_Resistor pull_resistor_2 (.node(In2));
  SHIFT_main Shift (
    .Shift_Right(1'b0), .I4(In1[3]), .I3(In1[2]), .I2(In1[1]), .Shift_Left(1'b0), .I1(In1[0]),
    .Select_bits(priority_encoder_1_p3), .CLK(CLK), .CLR(Clear), .A4(Shift_a1[3]), .A3(Shift_a1[2]),
    .A2(Shift_a1[1]), .A1(Shift_a1[0]));
  // Priority_Encoder #(.select(2)) priority_encoder_1: pin names not known; wires that end beside it: LO, HI, priority_encoder_1_p3, 1'b1, SR, SL, SLO
  FULL_SUB__1__main u_Sub (.A(In1), .B(In2), .carryout(Carry), .out(Sub_out));  // open: Cin
  Multiplexer #(.select(3), .width(4)) multiplexer_1 (
    .in0(add_output_4), .in1(Sub_out), .in3(Shift_a1), .in4(Shift_a1), .in5(LO), .in7(4'b0000), .out(Out),
    .sel(priority_encoder_2_out), .en(E));  // open: in2, in6
  Priority_Encoder #(.disabled(0)) priority_encoder_2 (
    .in0(Add), .in1(Sub), .in2(SLO), .in3(SL), .in4(SR), .in5(Mul), .in6(S6), .in7(Clear),
    .out(priority_encoder_2_out));  // open: en_in
endmodule

// RegistorBank
module TempReg (
  input  E,
  input  [1:0] RS,
  input  [3:0] DI,
  input  CLK,
  input  RW,
  output [3:0] DO
);

  wire and_1_out, demultiplexer_1_out0, demultiplexer_1_out1, demultiplexer_1_out2, demultiplexer_1_out3,
       not_2_out;
  wire [3:0] and_2_out, multiplexer_1_out, not_1_out, register_1_q, register_2_q, register_3_q, register_4_q;

  Demultiplexer #(.select(2), .disabled(0)) demultiplexer_1 (
    .out0(demultiplexer_1_out0), .out1(demultiplexer_1_out1), .out2(demultiplexer_1_out2),
    .out3(demultiplexer_1_out3), .in(1'b1), .sel(RS), .en(E));
  and and_1 (and_1_out, CLK, not_2_out);
  Register #(.width(4)) register_1 (
    .D(and_2_out), .en(demultiplexer_1_out0), .Q(register_1_q), .clk(and_1_out), .clr(1'b0));
  Register #(.width(4)) register_2 (
    .D(and_2_out), .en(demultiplexer_1_out1), .Q(register_2_q), .clk(and_1_out), .clr(1'b0));
  Register #(.width(4)) register_3 (
    .D(and_2_out), .en(demultiplexer_1_out2), .Q(register_3_q), .clk(and_1_out), .clr(1'b0));
  Register #(.width(4)) register_4 (
    .D(and_2_out), .en(demultiplexer_1_out3), .Q(register_4_q), .clk(and_1_out), .clr(1'b0));
  assign and_2_out = DI & not_1_out;  // AND_Gate and_2, 4 bits wide
  assign not_1_out = ~{4{RW}};  // NOT_Gate not_1, 4 bits wide
  not not_2 (not_2_out, RW);
  Multiplexer #(.select(2), .width(4), .disabled(0)) multiplexer_1 (
    .in0(register_1_q), .in1(register_2_q), .in2(register_3_q), .in3(register_4_q), .out(multiplexer_1_out),
    .sel(RS), .en(E));
  assign DO = multiplexer_1_out & {4{RW}};  // AND_Gate and_3, 4 bits wide

  // Notes on the sheet:
  //   DI: pull=down
  //   DO: pull=down
  //   and_3 drives only 1 and floats otherwise
endmodule

module Registor (
  input  E,
  input  [3:0] DI,
  input  CLK,
  input  RW,
  output [3:0] DO
);

  wire and_1_out, not_2_out;
  wire [3:0] and_2_out, not_1_out, Reg_q;

  and and_1 (and_1_out, CLK, not_2_out);
  assign and_2_out = DI & not_1_out;  // AND_Gate and_2, 4 bits wide
  Register #(.width(4)) Reg (.D(and_2_out), .en(E), .Q(Reg_q), .clk(and_1_out));  // open: clr
  assign not_1_out = ~{4{RW}};  // NOT_Gate not_1, 4 bits wide
  not not_2 (not_2_out, RW);
  assign DO = Reg_q & {4{RW}};  // AND_Gate and_3, 4 bits wide

  // Notes on the sheet:
  //   CLK: pull=down
  //   and_3 drives only 1 and floats otherwise
endmodule

module Registor_1bit (
  input  E,
  input  RW,
  input  CLK,
  output Data
);

  wire Reg_q, undriven;

  Register #(.width(1)) Reg (.D(undriven), .en(E), .Q(Reg_q), .clk(CLK));  // open: clr
  Multiplexer multiplexer_1 (.in0(undriven), .in1(Reg_q), .out(Data), .en(RW));  // open: sel
endmodule
