// Logisim project multiplier.circ as structural Verilog: 1 circuit, main circuit main
// adder
module main (
  input  in_1,
  input  B3,
  input  B2,
  input  B1,
  input  B0,
  input  in_6,
  input  A0,
  input  A1,
  input  A2,
  input  in_10,
  input  A3,
  input  in_12,
  output C7,
  output C6,
  output C4,
  output C5,
  output C3,
  output C2,
  output C1,
  output C0
);

  wire [0:0] adder_3_cout;
  wire [2:0] and_15_out;
  wire [3:0] adder_2_cout, and_5_out, and_8_out, and_12_out;
  wire [3:1] adder_3_out;

  and and_1 (and_5_out[3], A3, B3);
  and and_2 (and_5_out[2], A3, B2);
  and and_3 (and_5_out[1], A3, B1);
  and and_4 (and_8_out[3], A2, B3);
  and and_5 (and_5_out[0], A3, B0);
  and and_6 (and_8_out[2], A2, B2);
  and and_7 (and_8_out[1], A2, B1);
  Adder #(.width(4)) adder_1 (.a(adder_2_cout), .b(and_5_out), .out({C6, C5, C4, C3}), .cin(in_12), .cout(C7));
  and and_8 (and_8_out[0], A2, B0);
  and and_9 (and_12_out[3], A1, B3);
  and and_10 (and_12_out[2], A1, B2);
  and and_11 (and_12_out[1], A1, B1);
  Adder #(.width(4)) adder_2 (
    .a({adder_3_out[1], adder_3_out[2], adder_3_out[3], adder_3_cout[0]}), .b(and_8_out),
    .out({adder_2_cout[2:0], C2}), .cin(in_10), .cout(adder_2_cout[3]));
  and and_12 (and_12_out[0], A1, B0);
  and and_13 (and_15_out[2], A0, B3);
  and and_14 (and_15_out[1], A0, B2);
  and and_15 (and_15_out[0], A0, B1);
  Adder #(.width(4)) adder_3 (
    .a({in_1, and_15_out}), .b(and_12_out), .out({adder_3_out, C1}), .cin(in_6), .cout(adder_3_cout[0]));
  and and_16 (C0, A0, B0);

  // Notes on the sheet:
  //   in_10: pull=down
  //   in_12: pull=down
  //   in_6: pull=down
  //   in_1: pull=down
endmodule
