// Logisim project ALU_MUX_mod.circ as structural Verilog
module _1_BIT_ADDER (
  input  A,
  input  B,
  input  CARRY__IN,
  output Sum,
  output CARRY_OUT
);

  wire and_1_out, and_2_out, xor_1_out;

  xor xor_1 (xor_1_out, A, B);
  and and_1 (and_1_out, xor_1_out, CARRY__IN);
  and and_2 (and_2_out, A, B);
  xor xor_2 (Sum, xor_1_out, CARRY__IN);
  or or_1 (CARRY_OUT, and_1_out, and_2_out);
endmodule

module _8_BIT_ADDER (
  input  in_1,
  input  [7:0] A_8,
  input  [7:0] B_8,
  output [7:0] Output,
  output OVER_FLOW
);

  wire n1_bit_adder_1_carry_out, n1_bit_adder_2_carry_out, n1_bit_adder_3_carry_out,
       n1_bit_adder_4_carry_out, n1_bit_adder_5_carry_out, n1_bit_adder_6_carry_out, n1_bit_adder_7_carry_out;

  _1_BIT_ADDER u_1_bit_adder_1 (
    .A(A_8[0]), .B(B_8[0]), .CARRY__IN(in_1), .CARRY_OUT(n1_bit_adder_1_carry_out), .Sum(Output[0]));
  _1_BIT_ADDER u_1_bit_adder_2 (
    .A(A_8[1]), .B(B_8[1]), .CARRY__IN(n1_bit_adder_1_carry_out), .CARRY_OUT(n1_bit_adder_2_carry_out),
    .Sum(Output[1]));
  _1_BIT_ADDER u_1_bit_adder_3 (
    .A(A_8[2]), .B(B_8[2]), .CARRY__IN(n1_bit_adder_2_carry_out), .CARRY_OUT(n1_bit_adder_3_carry_out),
    .Sum(Output[2]));
  _1_BIT_ADDER u_1_bit_adder_4 (
    .A(A_8[3]), .B(B_8[3]), .CARRY__IN(n1_bit_adder_3_carry_out), .CARRY_OUT(n1_bit_adder_4_carry_out),
    .Sum(Output[3]));
  _1_BIT_ADDER u_1_bit_adder_5 (
    .A(A_8[4]), .B(B_8[4]), .CARRY__IN(n1_bit_adder_4_carry_out), .CARRY_OUT(n1_bit_adder_5_carry_out),
    .Sum(Output[4]));
  _1_BIT_ADDER u_1_bit_adder_6 (
    .A(A_8[5]), .B(B_8[5]), .CARRY__IN(n1_bit_adder_5_carry_out), .CARRY_OUT(n1_bit_adder_6_carry_out),
    .Sum(Output[5]));
  _1_BIT_ADDER u_1_bit_adder_7 (
    .A(A_8[6]), .B(B_8[6]), .CARRY__IN(n1_bit_adder_6_carry_out), .CARRY_OUT(n1_bit_adder_7_carry_out),
    .Sum(Output[6]));
  _1_BIT_ADDER u_1_bit_adder_8 (
    .A(A_8[7]), .B(B_8[7]), .CARRY__IN(n1_bit_adder_7_carry_out), .CARRY_OUT(OVER_FLOW), .Sum(Output[7]));
endmodule

module MUX_ALU (
  input  in_1,
  input  [7:0] IN_A,
  input  [7:0] IN_B,
  input  in_4,
  input  [2:0] OP_CODE,
  output [7:0] OUT
);

  wire [7:0] adder_1_out;

  Adder adder_1 (.a(IN_A), .b(IN_B), .out(adder_1_out), .cin(in_1));  // open: cout
  Subtractor subtractor_1 ();  // open: a, b, out, bin, bout
  Multiplier multiplier_1 ();  // open: a, b, out, cin, cout
  Divider #(.width(4)) divider_1 ();  // open: a, b, out, upper, rem
  Multiplexer #(.select(3), .width(8)) multiplexer_1 (
    .in0(adder_1_out), .out(OUT), .sel(OP_CODE), .en(in_4));  // open: in1, in2, in3, in4, in5, in6, in7
endmodule
