// Logisim project CU_v1_0.circ as structural Verilog: 6 circuits, main circuit main
module main (
  input  PCRST,
  input  [2:0] Shift_Amount,
  output [7:0] out_3,
  output [7:0] out_4,
  output [19:0] out_5,
  output [7:0] out_6,
  output [3:0] out_7,
  output [7:0] out_8,
  output [7:0] out_9,
  output [7:0] out_10
);

  wire ACCE, ACCRW, ADD, ADDE, alu_1_p10, ALUC, ALUE, and_2_out, and_3_out, and_4_out, and_5_out, and_6_out,
       and_7_out, and_8_out, and_9_out, and_10_out, and_11_out, and_12_out, and_13_out, and_14_out,
       and_15_out, and_16_out, and_17_out, and_19_out, buffer_34_out, CLK, CRE, CRRW, DME, DMRW, EXIT, HIE,
       HIRW, IME, INSEND, Instrustion_Decoder_out_210, Instrustion_Decoder_out_236, L1E, L2E, L3E, L4E, L5E,
       L6E, L7E, L8E, LLS, LOAD_ADDRESS, LOAD_CARRY, LOAD_HI, LOAD_IMMEDIATE, LOAD_LO, LOE, LORW, LRS, MOVE,
       MUL, MULE, nor_1_out, not_1_out, not_4_out, not_5_out, not_6_out, not_8_out, not_9_out, not_15_out,
       not_16_out, not_19_out, not_20_out, not_22_out, not_25_out, not_26_out, not_27_out, not_32_out,
       not_36_out, not_37_out, PCE, pull_resistor_4_node, ROE, RORW, RSTINS, s_r_ff_1_q, shift_register_1_q0,
       shift_register_1_q1, shift_register_1_q2, shift_register_2_q0, shift_register_2_q1,
       shift_register_2_q2, shift_register_3_q0, shift_register_3_q1, shift_register_3_q2,
       shift_register_4_q0, shift_register_4_q1, shift_register_4_q2, shift_register_5_q0,
       shift_register_5_q1, shift_register_5_q2, shift_register_5_q3, shift_register_5_q4,
       shift_register_6_q0, shift_register_6_q1, shift_register_6_q2, shift_register_7_q0,
       shift_register_7_q1, shift_register_7_q2, shift_register_7_q3, shift_register_7_q4,
       shift_register_7_q5, shift_register_7_q6, shift_register_8_q0, shift_register_8_q1,
       shift_register_8_q2, shift_register_8_q4, shift_register_8_q5, shift_register_8_q6,
       shift_register_8_q7, shift_register_9_q0, shift_register_9_q1, shift_register_9_q2,
       shift_register_10_q1, shift_register_10_q2, shift_register_10_q3, shift_register_10_q4,
       shift_register_10_q5, shift_register_11_q0, shift_register_11_q1, shift_register_11_q2, SHL, SLE, SRE,
       STORE, SUB, SUBE, TRE, TRRW, undriven;
  wire [3:0] L1, L1A_out, L1B_out, L2_out, L2_out_2, L3, not_28_out;
  wire [7:0] adder_1_out, alu_1_p14, alu_1_p15, and_1_out;
  wire [7:7] alu_1_p13;

  Pull_Resistor pull_resistor_1 (.node(out_8));
  assign out_7 = L1 | L3;  // OR_Gate or_1, 4 bits wide
  buf buffer_1 (DME, and_2_out);
  buf buffer_2 (L2E, and_6_out);
  buf buffer_3 (TRRW, and_6_out);
  Adder adder_1 (.a(out_3), .b(8'h1), .out(adder_1_out));  // open: cin, cout
  assign and_1_out = adder_1_out & {8{PCE}};  // AND_Gate and_1, 8 bits wide
  // TempReg tempreg_1: pin names not known; wires that end beside it: out_6, out_6, TRRW, CLK, TRE, out_7
  Registor ACC (.E(ACCE), .CLK(CLK), .DO(out_8), .RW(ACCRW), .DI(out_8));
  assign out_8 = out_6 & {8{L4E}};  // AND_Gate L4, 8 bits wide
  Shift_Register #(.length(3)) shift_register_1 (
    .shift(STORE), .in(1'b1), .clk(CLK), .clr(RSTINS), .q0(shift_register_1_q0), .q1(shift_register_1_q1),
    .q2(shift_register_1_q2));  // open: out, load, d0, d1, d2
  not not_1 (not_1_out, shift_register_1_q1);
  and and_2 (and_2_out, shift_register_1_q0, not_1_out);
  buf buffer_4 (L3E, and_2_out);
  not not_2 (DMRW, and_2_out);
  buf buffer_5 (DME, and_3_out);
  buf buffer_6 (DMRW, and_3_out);
  buf buffer_7 (CRRW, and_4_out);
  buf buffer_8 (CRE, and_4_out);
  buf buffer_9 (LOE, and_5_out);
  buf buffer_10 (LORW, and_5_out);
  buf buffer_11 (ACCE, and_6_out);
  not not_3 (L1E, and_6_out);
  buf buffer_12 (L4E, and_6_out);
  buf buffer_13 (TRE, and_6_out);
  Register register_1 (.D(and_1_out), .en(PCE), .Q(out_3), .clk(CLK), .clr(PCRST));
  assign out_6 = {8{L8E}} & out_8;  // AND_Gate L8, 8 bits wide
  buf buffer_14 (INSEND, shift_register_1_q2);
  buf buffer_15 (TRE, and_2_out);
  buf buffer_16 (TRRW, and_2_out);
  Shift_Register #(.length(3)) shift_register_2 (
    .shift(LOAD_ADDRESS), .in(1'b1), .clk(CLK), .clr(RSTINS), .q0(shift_register_2_q0),
    .q1(shift_register_2_q1), .q2(shift_register_2_q2));  // open: out, load, d0, d1, d2
  not not_4 (not_4_out, shift_register_2_q1);
  and and_3 (and_3_out, shift_register_2_q0, not_4_out);
  buf buffer_17 (L3E, and_3_out);
  buf buffer_18 (TRE, and_3_out);
  Shift_Register #(.length(3)) shift_register_3 (
    .shift(LOAD_CARRY), .in(1'b1), .clk(CLK), .clr(RSTINS), .q0(shift_register_3_q0),
    .q1(shift_register_3_q1), .q2(shift_register_3_q2));  // open: out, load, d0, d1, d2
  not not_5 (not_5_out, shift_register_3_q1);
  and and_4 (and_4_out, shift_register_3_q0, not_5_out);
  buf buffer_19 (TRE, and_4_out);
  buf buffer_20 (L3E, and_4_out);
  Shift_Register #(.length(3)) shift_register_4 (
    .shift(LOAD_LO), .in(1'b1), .clk(CLK), .clr(RSTINS), .q0(shift_register_4_q0), .q1(shift_register_4_q1),
    .q2(shift_register_4_q2));  // open: out, load, d0, d1, d2
  buf buffer_21 (INSEND, shift_register_4_q2);
  not not_6 (not_6_out, shift_register_4_q1);
  and and_5 (and_5_out, shift_register_4_q0, not_6_out);
  not not_7 (TRRW, and_5_out);
  buf buffer_22 (L3E, and_5_out);
  buf buffer_23 (TRE, and_5_out);
  Shift_Register #(.length(5)) shift_register_5 (
    .shift(MOVE), .in(1'b1), .clk(CLK), .clr(RSTINS), .q0(shift_register_5_q0), .q1(shift_register_5_q1),
    .q2(shift_register_5_q2), .q3(shift_register_5_q3), .q4(shift_register_5_q4));  // open: out, load, d0, d1, d2, d3, d4
  not not_8 (not_8_out, shift_register_5_q3);
  not not_9 (not_9_out, shift_register_5_q1);
  and and_6 (and_6_out, shift_register_5_q0, not_9_out);
  and and_7 (and_7_out, shift_register_5_q2, not_8_out);
  not not_10 (ACCRW, and_6_out);
  buf buffer_24 (ACCE, and_7_out);
  Decoder Instrustion_Decoder (
    .M0(out_5[12]), .M1(out_5[13]), .M2(out_5[14]), .M3(out_5[15]), .M4(out_5[16]), .M5(out_5[17]),
    .M6(out_5[18]), .M7(out_5[19]), .out_236(Instrustion_Decoder_out_236),
    .out_239(Instrustion_Decoder_out_236), .out_210(Instrustion_Decoder_out_210),
    .out_224(Instrustion_Decoder_out_210), .out_41(LOAD_LO), .out_42(LOAD_IMMEDIATE), .out_43(STORE),
    .out_44(ADD), .out_45(SUB), .out_46(LRS), .out_47(LLS), .out_48(MUL), .out_49(LOAD_HI),
    .out_50(LOAD_ADDRESS), .out_51(MOVE), .out_52(LOAD_CARRY), .out_53(EXIT));  // open: out_233, out_234, out_235, out_237, out_238, out_240, out_241, out_242, out_243, out_244, out_245, out_246, out_247, out_248, out_249, out_250, out_251, out_252, out_253, out_254, out_255, out_256, out_257, out_258, out_259, out_260, out_261, out_262, out_263, out_264, out_201, out_202, out_203, out_204, out_205, out_206, out_207, out_208, out_209, out_211, out_212, out_213, out_214, out_215, out_216, out_217, out_218, out_219, out_220, out_221, out_222, out_223, out_225, out_226, out_227, out_228, out_229, out_230, out_231, out_232, out_169, out_170, out_171, out_172, out_173, out_174, out_175, out_176, out_177, out_178, out_179, out_180, out_181, out_182, out_183, out_184, out_185, out_186, out_187, out_188, out_189, out_190, out_191, out_192, out_193, out_194, out_195, out_196, out_197, out_198, out_199, out_200, out_137, out_138, out_139, out_140, out_141, out_142, out_143, out_144, out_145, out_146, out_147, out_148, out_149, out_150, out_151, out_152, out_153, out_154, out_155, out_156, out_157, out_158, out_159, out_160, out_161, out_162, out_163, out_164, out_165, out_166, out_167, out_168, out_105, out_106, out_107, out_108, out_109, out_110, out_111, out_112, out_113, out_114, out_115, out_116, out_117, out_118, out_119, out_120, out_121, out_122, out_123, out_124, out_125, out_126, out_127, out_128, out_129, out_130, out_131, out_132, out_133, out_134, out_135, out_136, out_73, out_74, out_75, out_76, out_77, out_78, out_79, out_80, out_81, out_82, out_83, out_84, out_85, out_86, out_87, out_88, out_89, out_90, out_91, out_92, out_93, out_94, out_95, out_96, out_97, out_98, out_99, out_100, out_101, out_102, out_103, out_104, out_54, out_55, out_56, out_57, out_58, out_59, out_60, out_61, out_62, out_63, out_64, out_65, out_66, out_67, out_68, out_69, out_70, out_71, out_72, Output_1, out_10, out_11, out_12, out_13, out_14, out_15, out_16, out_17, out_18, out_19, out_20, out_21, out_22, out_23, out_24, out_25, out_26, out_27, out_28, out_29, out_30, out_31, out_32, out_33, out_34, out_35, out_36, out_37, out_38, out_39, out_40
  Pull_Resistor pull_resistor_2 (.node(out_6));
  assign out_6 = {8{alu_1_p13[7]}} & {8{L6E}};  // AND_Gate L6, 8 bits wide
  buf buffer_25 (INSEND, shift_register_2_q2);
  not not_11 (TRRW, and_3_out);
  buf buffer_26 (INSEND, shift_register_3_q2);
  not not_12 (TRRW, and_4_out);
  buf buffer_27 (ACCE, and_8_out);
  buf buffer_28 (ACCE, and_10_out);
  buf buffer_29 (CRRW, and_9_out);
  buf buffer_30 (INSEND, shift_register_5_q4);
  buf buffer_31 (TRE, and_7_out);
  not not_13 (TRRW, and_7_out);
  buf buffer_32 (L3E, and_7_out);
  buf buffer_33 (L8E, and_7_out);
  assign out_6 = {8{L7E}} & out_4;  // AND_Gate L7, 8 bits wide
  // ALU alu_1: pin names not known; wires that end beside it: ADDE, SUBE, SHL, SLE, SRE, MULE, ALUC, ALUE, out_8, alu_1_p10, out_6, out_10, alu_1_p13[7], alu_1_p14, alu_1_p15
  buf buffer_34 (buffer_34_out, MUL);
  buf buffer_35 (buffer_34_out, SUB);
  buf buffer_36 (buffer_34_out, ADD);
  not not_14 (L1E, and_8_out);
  buf buffer_37 (L2E, and_8_out);
  buf buffer_38 (TRRW, and_8_out);
  buf buffer_39 (L2E, and_10_out);
  buf buffer_40 (ACCRW, and_10_out);
  Shift_Register #(.length(3)) shift_register_6 (
    .shift(LOAD_CARRY), .in(1'b1), .clk(CLK), .clr(RSTINS), .q0(shift_register_6_q0),
    .q1(shift_register_6_q1), .q2(shift_register_6_q2));  // open: out, load, d0, d1, d2
  buf buffer_41 (L3E, and_9_out);
  buf buffer_42 (CRE, and_9_out);
  buf buffer_43 (ACCRW, and_7_out);
  assign out_6 = {8{L5E}} & out_10;  // AND_Gate L5, 8 bits wide
  Registor CARRY (.E(CRE), .CLK(CLK), .DO({8{alu_1_p13[7]}}), .RW(CRRW), .DI({8{alu_1_p13[7]}}));
  Registor HI (.E(HIE), .CLK(CLK), .DO(alu_1_p15), .RW(HIRW));  // open: DI
  Pull_Resistor pull_resistor_3 (.node(buffer_34_out));
  Shift_Register #(.length(7)) shift_register_7 (
    .shift(buffer_34_out), .in(1'b1), .clk(CLK), .clr(RSTINS), .q0(shift_register_7_q0),
    .q1(shift_register_7_q1), .q2(shift_register_7_q2), .q3(shift_register_7_q3), .q4(shift_register_7_q4),
    .q5(shift_register_7_q5), .q6(shift_register_7_q6));  // open: out, load, d0, d1, d2, d3, d4, d5, d6
  not not_15 (not_15_out, shift_register_7_q1);
  and and_8 (and_8_out, shift_register_7_q0, not_15_out);
  buf buffer_44 (TRE, and_8_out);
  buf buffer_45 (L4E, and_8_out);
  buf buffer_46 (TRE, and_10_out);
  buf buffer_47 (L1E, and_10_out);
  buf buffer_48 (INSEND, shift_register_6_q2);
  not not_16 (not_16_out, shift_register_6_q1);
  and and_9 (and_9_out, shift_register_6_q0, not_16_out);
  not not_17 (TRRW, and_9_out);
  buf buffer_49 (TRE, and_9_out);
  not not_18 (L1E, and_11_out);
  buf buffer_50 (TRE, and_11_out);
  buf buffer_51 (TRRW, and_11_out);
  buf buffer_52 (ALUE, and_11_out);
  buf buffer_53 (TRRW, and_14_out);
  assign L3 = out_5[11:8] & {4{L3E}};  // AND_Gate L3, 4 bits wide
  Registor OR_2 (.E(ROE), .CLK(CLK), .DO(out_10), .RW(RORW), .DI(out_10));
  Registor LO (.E(LOE), .CLK(CLK), .DO(alu_1_p14), .RW(LORW));  // open: DI
  buf buffer_54 (INSEND, shift_register_7_q6);
  not not_19 (not_19_out, shift_register_7_q5);
  not not_20 (not_20_out, shift_register_7_q3);
  not not_21 (ACCRW, and_8_out);
  and and_10 (and_10_out, shift_register_7_q2, not_20_out);
  buf buffer_55 (TRRW, and_10_out);
  buf buffer_56 (CRE, and_10_out);
  buf buffer_57 (HIRW, and_13_out);
  buf buffer_58 (HIE, and_13_out);
  Pull_Resistor pull_resistor_4 (.node(pull_resistor_4_node));
  buf buffer_59 (pull_resistor_4_node, LRS);
  buf buffer_60 (pull_resistor_4_node, LLS);
  Shift_Register shift_register_8 (
    .shift(pull_resistor_4_node), .in(1'b1), .clk(CLK), .clr(RSTINS), .q0(shift_register_8_q0),
    .q1(shift_register_8_q1), .q2(shift_register_8_q2), .q4(shift_register_8_q4), .q5(shift_register_8_q5),
    .q6(shift_register_8_q6), .q7(shift_register_8_q7));  // open: out, load, d0, d1, d2, d3, q3, d4, d5, d6, d7
  not not_22 (not_22_out, shift_register_8_q1);
  buf buffer_61 (L2E, and_11_out);
  buf buffer_62 (SHL, and_11_out);
  and and_11 (and_11_out, shift_register_8_q0, not_22_out);
  not not_23 (RORW, and_14_out);
  buf buffer_63 (ROE, and_14_out);
  RAM ram_1 (.addr(out_4), .data(out_6), .sel(DME), .clk(CLK), .ld(DMRW));  // open: clr
  RAM #(.dataWidth(20)) ram_2 (.addr(out_3), .data({out_5[19:8], out_4}), .sel(IME), .clk(CLK), .ld(IME));  // open: clr
  Pull_Resistor pull_resistor_5 (.node(out_10));
  Pull_Resistor pull_resistor_6 (.node(PCE));
  Pull_Resistor pull_resistor_7 (.node(PCE));
  Pull_Resistor pull_resistor_8 (.node(INSEND));
  and and_12 (and_12_out, not_19_out, shift_register_7_q4);
  buf buffer_64 (L5E, and_12_out);
  buf buffer_65 (L3E, and_12_out);
  buf buffer_66 (TRE, and_12_out);
  not not_24 (CRRW, and_10_out);
  buf buffer_67 (ROE, and_10_out);
  Shift_Register #(.length(3)) shift_register_9 (
    .shift(LOAD_HI), .in(1'b1), .clk(CLK), .clr(RSTINS), .q0(shift_register_9_q0), .q1(shift_register_9_q1),
    .q2(shift_register_9_q2));  // open: out, load, d0, d1, d2
  not not_25 (not_25_out, shift_register_9_q1);
  and and_13 (and_13_out, shift_register_9_q0, not_25_out);
  buf buffer_68 (TRE, and_13_out);
  buf buffer_69 (L3E, and_13_out);
  not not_26 (not_26_out, shift_register_8_q4);
  not not_27 (not_27_out, shift_register_8_q6);
  and and_14 (and_14_out, shift_register_8_q2, not_26_out);
  and and_15 (and_15_out, and_14_out, LLS);
  and and_16 (and_16_out, and_14_out, LRS);
  buf buffer_70 (SRE, and_16_out);
  buf buffer_71 (SLE, and_15_out);
  Pull_Resistor pull_resistor_9 (.node({out_5[19:8], out_4}));
  Pull_Resistor pull_resistor_10 (.node(out_4));
  assign not_28_out = ~{4{L1E}};  // NOT_Gate not_28, 4 bits wide
  assign L1A_out = {4{L1E}} & L2_out;  // AND_Gate L1A, 4 bits wide
  assign L1 = L1A_out | L1B_out;  // OR_Gate or_3, 4 bits wide
  Pull_Resistor pull_resistor_11 (.node(ALUE));
  Pull_Resistor pull_resistor_12 (.node(ADDE));
  Pull_Resistor pull_resistor_13 (.node(SUBE));
  Pull_Resistor pull_resistor_14 (.node(SHL));
  Pull_Resistor pull_resistor_15 (.node(SLE));
  Pull_Resistor pull_resistor_16 (.node(SRE));
  Pull_Resistor pull_resistor_17 (.node(MULE));
  Pull_Resistor pull_resistor_18 (.node(ALUC));
  Pull_Resistor pull_resistor_19 (.node(HIE));
  Pull_Resistor pull_resistor_20 (.node(HIRW));
  Pull_Resistor pull_resistor_21 (.node(LOE));
  Pull_Resistor pull_resistor_22 (.node(LORW));
  S_R_Flip_Flop s_r_ff_1 (
    .S(INSEND), .clk(CLK), .R(shift_register_10_q4), .Q(s_r_ff_1_q), .en(not_36_out));  // open: Qn, preset, reset
  Shift_Register #(.length(6)) shift_register_10 (
    .shift(s_r_ff_1_q), .in(1'b1), .clk(CLK), .clr(undriven), .q0(RSTINS), .q1(shift_register_10_q1),
    .q2(shift_register_10_q2), .q3(shift_register_10_q3), .q4(shift_register_10_q4), .q5(shift_register_10_q5));  // open: out, load, d0, d1, d2, d3, d4, d5
  buf buffer_72 (RORW, and_12_out);
  buf buffer_73 (ROE, and_12_out);
  not not_29 (TRRW, and_12_out);
  buf buffer_74 (ALUE, and_10_out);
  not not_30 (RORW, and_10_out);
  buf buffer_75 (INSEND, shift_register_9_q2);
  not not_31 (TRRW, and_13_out);
  buf buffer_76 (INSEND, shift_register_8_q7);
  and and_17 (and_17_out, not_27_out, shift_register_8_q5);
  buf buffer_77 (L3E, and_17_out);
  buf buffer_78 (ALUE, and_14_out);
  buf buffer_79 (TRE, and_14_out);
  Clock u_CLK (.out(CLK));
  assign {L2_out, L2_out_2} = {8{L2E}} & out_4;  // AND_Gate L2, 8 bits wide
  assign L1B_out = L2_out_2 & not_28_out;  // AND_Gate L1B, 4 bits wide
  Pull_Resistor pull_resistor_23 (.node(L1E));
  Pull_Resistor pull_resistor_24 (.node(L2E));
  Pull_Resistor pull_resistor_25 (.node(L3E));
  Pull_Resistor pull_resistor_26 (.node(L4E));
  Pull_Resistor pull_resistor_27 (.node(L5E));
  Pull_Resistor pull_resistor_28 (.node(L6E));
  Pull_Resistor pull_resistor_29 (.node(L7E));
  Pull_Resistor pull_resistor_30 (.node(L8E));
  Pull_Resistor pull_resistor_31 (.node(IME));
  Pull_Resistor pull_resistor_32 (.node(IME));
  Pull_Resistor pull_resistor_33 (.node(DMRW));
  Pull_Resistor pull_resistor_34 (.node(DME));
  not not_32 (not_32_out, shift_register_10_q2);
  and and_18 (PCE, shift_register_10_q1, not_32_out);
  buf buffer_80 (LOE, and_10_out);
  not not_33 (HIRW, and_10_out);
  buf buffer_81 (HIE, and_10_out);
  not not_34 (LORW, and_10_out);
  Shift_Register #(.length(3)) shift_register_11 (
    .shift(LOAD_IMMEDIATE), .in(1'b1), .clk(CLK), .clr(RSTINS), .q0(shift_register_11_q0),
    .q1(shift_register_11_q1), .q2(shift_register_11_q2));  // open: out, load, d0, d1, d2
  buf buffer_82 (L7E, and_19_out);
  buf buffer_83 (L3E, and_19_out);
  buf buffer_84 (L5E, and_17_out);
  buf buffer_85 (RORW, and_17_out);
  not not_35 (TRRW, and_17_out);
  buf buffer_86 (TRE, and_17_out);
  not not_36 (not_36_out, shift_register_10_q5);
  nor nor_1 (nor_1_out, shift_register_10_q3, INSEND, IME);
  buf buffer_87 (INSEND, shift_register_11_q2);
  not not_37 (not_37_out, shift_register_11_q1);
  and and_19 (and_19_out, shift_register_11_q0, not_37_out);
  not not_38 (TRRW, and_19_out);
  buf buffer_88 (TRE, and_19_out);
  buf buffer_89 (ROE, and_17_out);
  Pull_Resistor pull_resistor_35 (.node(TRE));
  Pull_Resistor pull_resistor_36 (.node(TRRW));
  Pull_Resistor pull_resistor_37 (.node(CRRW));
  Pull_Resistor pull_resistor_38 (.node(CRE));
  Pull_Resistor pull_resistor_39 (.node(RORW));
  Pull_Resistor pull_resistor_40 (.node(ROE));
  Pull_Resistor pull_resistor_41 (.node(ACCRW));
  Pull_Resistor pull_resistor_42 (.node(ACCE));
  buf buffer_90 (ADDE, ADD);
  buf buffer_91 (SUBE, SUB);
  buf buffer_92 (MULE, MUL);
  S_R_Flip_Flop s_r_ff_2 (
    .S(shift_register_10_q3), .clk(CLK), .R(INSEND), .Q(IME), .preset(nor_1_out), .en(1'b1));  // open: Qn, reset

  assign out_5[7:0] = out_4;
  assign out_9 = out_6;
  // also tied to GND on the sheet: alu_1_p13[7]

  // Other names for the same wires on the sheet: PCIE = PCE; IMRW = IME; IMUX[7:0] = out_5[19:12]; TRS[3:0] = out_7

  // Notes on the sheet:
  //   buffer_1 drives only 1 and floats otherwise
  //   buffer_2 drives only 1 and floats otherwise
  //   buffer_3 drives only 1 and floats otherwise
  //   L4 drives only 1 and floats otherwise
  //   buffer_4 drives only 1 and floats otherwise
  //   not_2 drives only 0 and floats otherwise
  //   buffer_5 drives only 1 and floats otherwise
  //   buffer_6 drives only 1 and floats otherwise
  //   buffer_7 drives only 1 and floats otherwise
  //   buffer_8 drives only 1 and floats otherwise
  //   buffer_9 drives only 1 and floats otherwise
  //   buffer_10 drives only 1 and floats otherwise
  //   buffer_11 drives only 1 and floats otherwise
  //   not_3 drives only 0 and floats otherwise
  //   buffer_12 drives only 1 and floats otherwise
  //   buffer_13 drives only 1 and floats otherwise
  //   L8 drives only 1 and floats otherwise
  //   buffer_14 drives only 1 and floats otherwise
  //   buffer_15 drives only 1 and floats otherwise
  //   buffer_16 drives only 1 and floats otherwise
  //   buffer_17 drives only 1 and floats otherwise
  //   buffer_18 drives only 1 and floats otherwise
  //   buffer_19 drives only 1 and floats otherwise
  //   buffer_20 drives only 1 and floats otherwise
  //   buffer_21 drives only 1 and floats otherwise
  //   not_7 drives only 0 and floats otherwise
  //   buffer_22 drives only 1 and floats otherwise
  //   buffer_23 drives only 1 and floats otherwise
  //   not_10 drives only 0 and floats otherwise
  //   buffer_24 drives only 1 and floats otherwise
  //   L6 drives only 1 and floats otherwise
  //   buffer_25 drives only 1 and floats otherwise
  //   not_11 drives only 0 and floats otherwise
  //   buffer_26 drives only 1 and floats otherwise
  //   not_12 drives only 0 and floats otherwise
  //   buffer_27 drives only 1 and floats otherwise
  //   buffer_28 drives only 1 and floats otherwise
  //   buffer_29 drives only 1 and floats otherwise
  //   buffer_30 drives only 1 and floats otherwise
  //   buffer_31 drives only 1 and floats otherwise
  //   not_13 drives only 0 and floats otherwise
  //   buffer_32 drives only 1 and floats otherwise
  //   buffer_33 drives only 1 and floats otherwise
  //   L7 drives only 1 and floats otherwise
  //   buffer_34 drives only 1 and floats otherwise
  //   buffer_35 drives only 1 and floats otherwise
  //   buffer_36 drives only 1 and floats otherwise
  //   not_14 drives only 0 and floats otherwise
  //   buffer_37 drives only 1 and floats otherwise
  //   buffer_38 drives only 1 and floats otherwise
  //   buffer_39 drives only 1 and floats otherwise
  //   buffer_40 drives only 1 and floats otherwise
  //   buffer_41 drives only 1 and floats otherwise
  //   buffer_42 drives only 1 and floats otherwise
  //   buffer_43 drives only 1 and floats otherwise
  //   L5 drives only 1 and floats otherwise
  //   buffer_44 drives only 1 and floats otherwise
  //   buffer_45 drives only 1 and floats otherwise
  //   buffer_46 drives only 1 and floats otherwise
  //   buffer_47 drives only 1 and floats otherwise
  //   buffer_48 drives only 1 and floats otherwise
  //   not_17 drives only 0 and floats otherwise
  //   buffer_49 drives only 1 and floats otherwise
  //   not_18 drives only 0 and floats otherwise
  //   buffer_50 drives only 1 and floats otherwise
  //   buffer_51 drives only 1 and floats otherwise
  //   buffer_52 drives only 1 and floats otherwise
  //   buffer_53 drives only 1 and floats otherwise
  //   Data Memory
  //   Ins. Memory
  //   buffer_54 drives only 1 and floats otherwise
  //   not_21 drives only 0 and floats otherwise
  //   buffer_55 drives only 1 and floats otherwise
  //   buffer_56 drives only 1 and floats otherwise
  //   buffer_57 drives only 1 and floats otherwise
  //   buffer_58 drives only 1 and floats otherwise
  //   buffer_59 drives only 1 and floats otherwise
  //   buffer_60 drives only 1 and floats otherwise
  //   buffer_61 drives only 1 and floats otherwise
  //   buffer_62 drives only 1 and floats otherwise
  //   not_23 drives only 0 and floats otherwise
  //   buffer_63 drives only 1 and floats otherwise
  //   buffer_64 drives only 1 and floats otherwise
  //   buffer_65 drives only 1 and floats otherwise
  //   buffer_66 drives only 1 and floats otherwise
  //   not_24 drives only 0 and floats otherwise
  //   buffer_67 drives only 1 and floats otherwise
  //   buffer_68 drives only 1 and floats otherwise
  //   buffer_69 drives only 1 and floats otherwise
  //   buffer_70 drives only 1 and floats otherwise
  //   buffer_71 drives only 1 and floats otherwise
  //   buffer_72 drives only 1 and floats otherwise
  //   buffer_73 drives only 1 and floats otherwise
  //   not_29 drives only 0 and floats otherwise
  //   buffer_74 drives only 1 and floats otherwise
  //   not_30 drives only 0 and floats otherwise
  //   buffer_75 drives only 1 and floats otherwise
  //   not_31 drives only 0 and floats otherwise
  //   buffer_76 drives only 1 and floats otherwise
  //   buffer_77 drives only 1 and floats otherwise
  //   buffer_78 drives only 1 and floats otherwise
  //   buffer_79 drives only 1 and floats otherwise
  //   and_18 drives only 1 and floats otherwise
  //   buffer_80 drives only 1 and floats otherwise
  //   not_33 drives only 0 and floats otherwise
  //   buffer_81 drives only 1 and floats otherwise
  //   not_34 drives only 0 and floats otherwise
  //   buffer_82 drives only 1 and floats otherwise
  //   buffer_83 drives only 1 and floats otherwise
  //   buffer_84 drives only 1 and floats otherwise
  //   buffer_85 drives only 1 and floats otherwise
  //   not_35 drives only 0 and floats otherwise
  //   buffer_86 drives only 1 and floats otherwise
  //   buffer_87 drives only 1 and floats otherwise
  //   not_38 drives only 0 and floats otherwise
  //   buffer_88 drives only 1 and floats otherwise
  //   buffer_89 drives only 1 and floats otherwise
  //   buffer_90 drives only 1 and floats otherwise
  //   buffer_91 drives only 1 and floats otherwise
  //   buffer_92 drives only 1 and floats otherwise
endmodule

module ALU (
  input  C,
  input  [7:0] In1,
  input  [7:0] In2,
  input  E,
  input  [7:0] Carry_In,
  input  [2:0] Shift_Amount,
  input  Add,
  input  Sub,
  input  SL,
  input  SR,
  input  Mul,
  input  S6,
  input  Clear,
  output Carry,
  output [7:0] Out,
  output [7:0] HI,
  output [7:0] LO
);

  wire [2:0] priority_encoder_1_out;
  wire [7:0] adder_1_out, shifter_1_out, shifter_2_out, subtractor_1_out;

  Multiplier multiplier_1 (.a(In1), .b(In2), .out(LO), .cin(Carry_In), .cout(HI));
  Adder adder_1 (.a(In2), .b(In1), .out(adder_1_out), .cin(C), .cout(Carry));
  Pull_Resistor pull_resistor_1 (.node(In1));
  Pull_Resistor pull_resistor_2 (.node(In2));
  Subtractor subtractor_1 (.a(In1), .b(In2), .out(subtractor_1_out), .bin(C), .bout(Carry));
  Shifter shifter_1 (.in(In1), .\dist (Shift_Amount), .out(shifter_1_out));
  Shifter #(.shift("lr")) shifter_2 (.in(In1), .\dist (Shift_Amount), .out(shifter_2_out));
  Multiplexer #(.select(3), .width(8)) multiplexer_1 (
    .in0(adder_1_out), .in1(subtractor_1_out), .in3(shifter_1_out), .in4(shifter_2_out), .in5(LO),
    .in7({8{1'b0}}), .out(Out), .sel(priority_encoder_1_out), .en(E));  // open: in2, in6
  Priority_Encoder #(.disabled(0)) priority_encoder_1 (
    .in0(Add), .in1(Sub), .in3(SL), .in4(SR), .in5(Mul), .in6(S6), .in7(Clear), .out(priority_encoder_1_out));  // open: in2, en_in
endmodule

// RegistorBank
module TempReg (
  input  E,
  input  [3:0] RS,
  input  [7:0] DI,
  input  CLK,
  input  RW,
  output [7:0] DO
);

  wire and_1_out, demultiplexer_1_out0, demultiplexer_1_out1, demultiplexer_1_out2, demultiplexer_1_out3,
       demultiplexer_1_out4, demultiplexer_1_out5, demultiplexer_1_out6, demultiplexer_1_out7,
       demultiplexer_1_out8, demultiplexer_1_out9, demultiplexer_1_out10, demultiplexer_1_out11,
       demultiplexer_1_out12, demultiplexer_1_out13, demultiplexer_1_out14, demultiplexer_1_out15, not_2_out;
  wire [7:0] and_2_out, multiplexer_1_out, not_1_out, register_1_q, register_2_q, register_3_q, register_4_q,
       register_5_q, register_6_q, register_7_q, register_8_q, register_9_q, register_10_q, register_11_q,
       register_12_q, register_13_q, register_14_q, register_15_q, register_16_q;

  Demultiplexer #(.select(4)) demultiplexer_1 (
    .out0(demultiplexer_1_out0), .out1(demultiplexer_1_out1), .out2(demultiplexer_1_out2),
    .out3(demultiplexer_1_out3), .out4(demultiplexer_1_out4), .out5(demultiplexer_1_out5),
    .out6(demultiplexer_1_out6), .out7(demultiplexer_1_out7), .out8(demultiplexer_1_out8),
    .out9(demultiplexer_1_out9), .out10(demultiplexer_1_out10), .out11(demultiplexer_1_out11),
    .out12(demultiplexer_1_out12), .out13(demultiplexer_1_out13), .out14(demultiplexer_1_out14),
    .out15(demultiplexer_1_out15), .sel(RS), .en(E));  // open: in
  and and_1 (and_1_out, CLK, not_2_out);
  assign and_2_out = DI & not_1_out;  // AND_Gate and_2, 8 bits wide
  assign not_1_out = ~{8{RW}};  // NOT_Gate not_1, 8 bits wide
  not not_2 (not_2_out, RW);
  Register register_1 (.D(and_2_out), .en(demultiplexer_1_out0), .Q(register_1_q), .clk(and_1_out), .clr(1'b0));
  Register register_2 (.D(and_2_out), .en(demultiplexer_1_out1), .Q(register_2_q), .clk(and_1_out), .clr(1'b0));
  Register register_3 (.D(and_2_out), .en(demultiplexer_1_out2), .Q(register_3_q), .clk(and_1_out), .clr(1'b0));
  Register register_4 (.D(and_2_out), .en(demultiplexer_1_out3), .Q(register_4_q), .clk(and_1_out), .clr(1'b0));
  Register register_5 (.D(and_2_out), .en(demultiplexer_1_out4), .Q(register_5_q), .clk(and_1_out), .clr(1'b0));
  Register register_6 (.D(and_2_out), .en(demultiplexer_1_out5), .Q(register_6_q), .clk(and_1_out), .clr(1'b0));
  Register register_7 (.D(and_2_out), .en(demultiplexer_1_out6), .Q(register_7_q), .clk(and_1_out), .clr(1'b0));
  Register register_8 (.D(and_2_out), .en(demultiplexer_1_out7), .Q(register_8_q), .clk(and_1_out), .clr(1'b0));
  Register register_9 (.D(and_2_out), .en(demultiplexer_1_out8), .Q(register_9_q), .clk(and_1_out), .clr(1'b0));
  Register register_10 (.D(and_2_out), .en(demultiplexer_1_out9), .Q(register_10_q), .clk(and_1_out), .clr(1'b0));
  Register register_11 (.D(and_2_out), .en(demultiplexer_1_out10), .Q(register_11_q), .clk(and_1_out), .clr(1'b0));
  Register register_12 (.D(and_2_out), .en(demultiplexer_1_out11), .Q(register_12_q), .clk(and_1_out), .clr(1'b0));
  Register register_13 (.D(and_2_out), .en(demultiplexer_1_out12), .Q(register_13_q), .clk(and_1_out), .clr(1'b0));
  Register register_14 (.D(and_2_out), .en(demultiplexer_1_out13), .Q(register_14_q), .clk(and_1_out), .clr(1'b0));
  Register register_15 (.D(and_2_out), .en(demultiplexer_1_out14), .Q(register_15_q), .clk(and_1_out), .clr(1'b0));
  Register register_16 (.D(and_2_out), .en(demultiplexer_1_out15), .Q(register_16_q), .clk(and_1_out), .clr(1'b0));
  assign DO = multiplexer_1_out & {8{RW}};  // AND_Gate and_3, 8 bits wide
  Multiplexer #(.select(4), .width(8)) multiplexer_1 (
    .in0(register_1_q), .in1(register_2_q), .in2(register_3_q), .in3(register_4_q), .in4(register_5_q),
    .in5(register_6_q), .in6(register_7_q), .in7(register_8_q), .in8(register_9_q), .in9(register_10_q),
    .in10(register_11_q), .in11(register_12_q), .in12(register_13_q), .in13(register_14_q),
    .in14(register_15_q), .in15(register_16_q), .out(multiplexer_1_out), .sel(RS), .en(E));

  // Notes on the sheet:
  //   DI: pull=down
  //   DO: pull=down
  //   and_3 drives only 1 and floats otherwise
endmodule

module Registor (
  input  E,
  input  [7:0] DI,
  input  CLK,
  input  RW,
  output [7:0] DO
);

  wire and_1_out, not_2_out;
  wire [7:0] and_2_out, not_1_out, Reg_q;

  and and_1 (and_1_out, CLK, not_2_out);
  assign and_2_out = DI & not_1_out;  // AND_Gate and_2, 8 bits wide
  Register Reg (.D(and_2_out), .en(E), .Q(Reg_q), .clk(and_1_out));  // open: clr
  assign not_1_out = ~{8{RW}};  // NOT_Gate not_1, 8 bits wide
  not not_2 (not_2_out, RW);
  assign DO = Reg_q & {8{RW}};  // AND_Gate and_3, 8 bits wide

  // Notes on the sheet:
  //   CLK: pull=down
  //   and_3 drives only 1 and floats otherwise
endmodule

module Registor_1bit (
  input  E,
  input  RW,
  input  CLK,
  output Data
);

  wire Reg_q, undriven;

  Register #(.width(1)) Reg (.D(undriven), .en(E), .Q(Reg_q), .clk(CLK));  // open: clr
  Multiplexer multiplexer_1 (.in0(undriven), .in1(Reg_q), .out(Data), .en(RW));  // open: sel
endmodule

module Decoder (
  input  M0,
  input  M1,
  input  M2,
  input  M3,
  input  M4,
  input  M5,
  input  M6,
  input  M7,
  output Output_1,
  output out_10,
  output out_11,
  output out_12,
  output out_13,
  output out_14,
  output out_15,
  output out_16,
  output out_17,
  output out_18,
  output out_19,
  output out_20,
  output out_21,
  output out_22,
  output out_23,
  output out_24,
  output out_25,
  output out_26,
  output out_27,
  output out_28,
  output out_29,
  output out_30,
  output out_31,
  output out_32,
  output out_33,
  output out_34,
  output out_35,
  output out_36,
  output out_37,
  output out_38,
  output out_39,
  output out_40,
  output out_41,
  output out_42,
  output out_43,
  output out_44,
  output out_45,
  output out_46,
  output out_47,
  output out_48,
  output out_49,
  output out_50,
  output out_51,
  output out_52,
  output out_53,
  output out_54,
  output out_55,
  output out_56,
  output out_57,
  output out_58,
  output out_59,
  output out_60,
  output out_61,
  output out_62,
  output out_63,
  output out_64,
  output out_65,
  output out_66,
  output out_67,
  output out_68,
  output out_69,
  output out_70,
  output out_71,
  output out_72,
  output out_73,
  output out_74,
  output out_75,
  output out_76,
  output out_77,
  output out_78,
  output out_79,
  output out_80,
  output out_81,
  output out_82,
  output out_83,
  output out_84,
  output out_85,
  output out_86,
  output out_87,
  output out_88,
  output out_89,
  output out_90,
  output out_91,
  output out_92,
  output out_93,
  output out_94,
  output out_95,
  output out_96,
  output out_97,
  output out_98,
  output out_99,
  output out_100,
  output out_101,
  output out_102,
  output out_103,
  output out_104,
  output out_105,
  output out_106,
  output out_107,
  output out_108,
  output out_109,
  output out_110,
  output out_111,
  output out_112,
  output out_113,
  output out_114,
  output out_115,
  output out_116,
  output out_117,
  output out_118,
  output out_119,
  output out_120,
  output out_121,
  output out_122,
  output out_123,
  output out_124,
  output out_125,
  output out_126,
  output out_127,
  output out_128,
  output out_129,
  output out_130,
  output out_131,
  output out_132,
  output out_133,
  output out_134,
  output out_135,
  output out_136,
  output out_137,
  output out_138,
  output out_139,
  output out_140,
  output out_141,
  output out_142,
  output out_143,
  output out_144,
  output out_145,
  output out_146,
  output out_147,
  output out_148,
  output out_149,
  output out_150,
  output out_151,
  output out_152,
  output out_153,
  output out_154,
  output out_155,
  output out_156,
  output out_157,
  output out_158,
  output out_159,
  output out_160,
  output out_161,
  output out_162,
  output out_163,
  output out_164,
  output out_165,
  output out_166,
  output out_167,
  output out_168,
  output out_169,
  output out_170,
  output out_171,
  output out_172,
  output out_173,
  output out_174,
  output out_175,
  output out_176,
  output out_177,
  output out_178,
  output out_179,
  output out_180,
  output out_181,
  output out_182,
  output out_183,
  output out_184,
  output out_185,
  output out_186,
  output out_187,
  output out_188,
  output out_189,
  output out_190,
  output out_191,
  output out_192,
  output out_193,
  output out_194,
  output out_195,
  output out_196,
  output out_197,
  output out_198,
  output out_199,
  output out_200,
  output out_201,
  output out_202,
  output out_203,
  output out_204,
  output out_205,
  output out_206,
  output out_207,
  output out_208,
  output out_209,
  output out_210,
  output out_211,
  output out_212,
  output out_213,
  output out_214,
  output out_215,
  output out_216,
  output out_217,
  output out_218,
  output out_219,
  output out_220,
  output out_221,
  output out_222,
  output out_223,
  output out_224,
  output out_225,
  output out_226,
  output out_227,
  output out_228,
  output out_229,
  output out_230,
  output out_231,
  output out_232,
  output out_233,
  output out_234,
  output out_235,
  output out_236,
  output out_237,
  output out_238,
  output out_239,
  output out_240,
  output out_241,
  output out_242,
  output out_243,
  output out_244,
  output out_245,
  output out_246,
  output out_247,
  output out_248,
  output out_249,
  output out_250,
  output out_251,
  output out_252,
  output out_253,
  output out_254,
  output out_255,
  output out_256,
  output out_257,
  output out_258,
  output out_259,
  output out_260,
  output out_261,
  output out_262,
  output out_263,
  output out_264
);

  wire decoder_1_out0, decoder_1_out1, decoder_1_out2, decoder_1_out3, decoder_1_out4, decoder_1_out5,
       decoder_1_out6, decoder_1_out7;

  Decoder_part #(.select(3)) decoder_1 (
    .out0(decoder_1_out0), .out1(decoder_1_out1), .out2(decoder_1_out2), .out3(decoder_1_out3),
    .out4(decoder_1_out4), .out5(decoder_1_out5), .out6(decoder_1_out6), .out7(decoder_1_out7),
    .sel({M7, M6, M5}));  // open: en
  Decoder_part #(.select(5)) decoder_2 (
    .out0(Output_1), .out1(out_10), .out2(out_11), .out3(out_12), .out4(out_13), .out5(out_14),
    .out6(out_15), .out7(out_16), .out8(out_17), .out9(out_18), .out10(out_19), .out11(out_20),
    .out12(out_21), .out13(out_22), .out14(out_23), .out15(out_24), .out16(out_25), .out17(out_26),
    .out18(out_27), .out19(out_28), .out20(out_29), .out21(out_30), .out22(out_31), .out23(out_32),
    .out24(out_33), .out25(out_34), .out26(out_35), .out27(out_36), .out28(out_37), .out29(out_38),
    .out30(out_39), .out31(out_40), .sel({M4, M3, M2, M1, M0}), .en(decoder_1_out0));
  Decoder_part #(.select(5)) decoder_3 (
    .out0(out_41), .out1(out_42), .out2(out_43), .out3(out_44), .out4(out_45), .out5(out_46), .out6(out_47),
    .out7(out_48), .out8(out_49), .out9(out_50), .out10(out_51), .out11(out_52), .out12(out_53),
    .out13(out_54), .out14(out_55), .out15(out_56), .out16(out_57), .out17(out_58), .out18(out_59),
    .out19(out_60), .out20(out_61), .out21(out_62), .out22(out_63), .out23(out_64), .out24(out_65),
    .out25(out_66), .out26(out_67), .out27(out_68), .out28(out_69), .out29(out_70), .out30(out_71),
    .out31(out_72), .sel({M4, M3, M2, M1, M0}), .en(decoder_1_out1));
  Decoder_part #(.select(5)) decoder_4 (
    .out0(out_73), .out1(out_74), .out2(out_75), .out3(out_76), .out4(out_77), .out5(out_78), .out6(out_79),
    .out7(out_80), .out8(out_81), .out9(out_82), .out10(out_83), .out11(out_84), .out12(out_85),
    .out13(out_86), .out14(out_87), .out15(out_88), .out16(out_89), .out17(out_90), .out18(out_91),
    .out19(out_92), .out20(out_93), .out21(out_94), .out22(out_95), .out23(out_96), .out24(out_97),
    .out25(out_98), .out26(out_99), .out27(out_100), .out28(out_101), .out29(out_102), .out30(out_103),
    .out31(out_104), .sel({M4, M3, M2, M1, M0}), .en(decoder_1_out2));
  Decoder_part #(.select(5)) decoder_5 (
    .out0(out_105), .out1(out_106), .out2(out_107), .out3(out_108), .out4(out_109), .out5(out_110),
    .out6(out_111), .out7(out_112), .out8(out_113), .out9(out_114), .out10(out_115), .out11(out_116),
    .out12(out_117), .out13(out_118), .out14(out_119), .out15(out_120), .out16(out_121), .out17(out_122),
    .out18(out_123), .out19(out_124), .out20(out_125), .out21(out_126), .out22(out_127), .out23(out_128),
    .out24(out_129), .out25(out_130), .out26(out_131), .out27(out_132), .out28(out_133), .out29(out_134),
    .out30(out_135), .out31(out_136), .sel({M4, M3, M2, M1, M0}), .en(decoder_1_out3));
  Decoder_part #(.select(5)) decoder_6 (
    .out0(out_137), .out1(out_138), .out2(out_139), .out3(out_140), .out4(out_141), .out5(out_142),
    .out6(out_143), .out7(out_144), .out8(out_145), .out9(out_146), .out10(out_147), .out11(out_148),
    .out12(out_149), .out13(out_150), .out14(out_151), .out15(out_152), .out16(out_153), .out17(out_154),
    .out18(out_155), .out19(out_156), .out20(out_157), .out21(out_158), .out22(out_159), .out23(out_160),
    .out24(out_161), .out25(out_162), .out26(out_163), .out27(out_164), .out28(out_165), .out29(out_166),
    .out30(out_167), .out31(out_168), .sel({M4, M3, M2, M1, M0}), .en(decoder_1_out4));
  Decoder_part #(.select(5)) decoder_7 (
    .out0(out_169), .out1(out_170), .out2(out_171), .out3(out_172), .out4(out_173), .out5(out_174),
    .out6(out_175), .out7(out_176), .out8(out_177), .out9(out_178), .out10(out_179), .out11(out_180),
    .out12(out_181), .out13(out_182), .out14(out_183), .out15(out_184), .out16(out_185), .out17(out_186),
    .out18(out_187), .out19(out_188), .out20(out_189), .out21(out_190), .out22(out_191), .out23(out_192),
    .out24(out_193), .out25(out_194), .out26(out_195), .out27(out_196), .out28(out_197), .out29(out_198),
    .out30(out_199), .out31(out_200), .sel({M4, M3, M2, M1, M0}), .en(decoder_1_out5));
  Decoder_part #(.select(5)) decoder_8 (
    .out0(out_201), .out1(out_202), .out2(out_203), .out3(out_204), .out4(out_205), .out5(out_206),
    .out6(out_207), .out7(out_208), .out8(out_209), .out9(out_210), .out10(out_211), .out11(out_212),
    .out12(out_213), .out13(out_214), .out14(out_215), .out15(out_216), .out16(out_217), .out17(out_218),
    .out18(out_219), .out19(out_220), .out20(out_221), .out21(out_222), .out22(out_223), .out23(out_224),
    .out24(out_225), .out25(out_226), .out26(out_227), .out27(out_228), .out28(out_229), .out29(out_230),
    .out30(out_231), .out31(out_232), .en(decoder_1_out6));  // open: sel
  Decoder_part #(.select(5)) decoder_9 (
    .out0(out_233), .out1(out_234), .out2(out_235), .out3(out_236), .out4(out_237), .out5(out_238),
    .out6(out_239), .out7(out_240), .out8(out_241), .out9(out_242), .out10(out_243), .out11(out_244),
    .out12(out_245), .out13(out_246), .out14(out_247), .out15(out_248), .out16(out_249), .out17(out_250),
    .out18(out_251), .out19(out_252), .out20(out_253), .out21(out_254), .out22(out_255), .out23(out_256),
    .out24(out_257), .out25(out_258), .out26(out_259), .out27(out_260), .out28(out_261), .out29(out_262),
    .out30(out_263), .out31(out_264), .sel({M4, M3, M2, M1, M0}), .en(decoder_1_out7));
endmodule
