// Logisim project CU_v3_0.circ as structural Verilog: 6 circuits, main circuit ALU
module main (
  input  PCRST,
  input  [2:0] Shift_Amount,
  output [7:0] out_3,
  output [7:0] out_4,
  output [19:0] out_5,
  output [7:0] out_6,
  output [3:0] out_7,
  output [7:0] out_8,
  output [7:0] out_9,
  output [7:0] out_10
);

  wire ACCE, ACCRW, ADD, ADDE, alu_1_p10, ALUC, ALUE, and_2_out, and_3_out, and_4_out, and_5_out, and_6_out,
       and_7_out, and_8_out, and_9_out, and_10_out, and_11_out, and_12_out, and_13_out, and_14_out,
       and_15_out, and_16_out, and_17_out, and_19_out, buffer_34_out, buffer_59_out, CLK, CRE, CRRW, DME,
       DMRW, EXIT, HIE, HIRW, IME, INSEND, L1E, L2E, L3E, L4E, L5E, L6E, L7E, L8E, LLS, LOAD_ADDRESS,
       LOAD_CARRY, LOAD_HI, LOAD_IMMEDIATE, LOAD_LO, LOE, LORW, LRS, MOVE, MUL, MULE, nor_1_out, not_1_out,
       not_4_out, not_5_out, not_6_out, not_8_out, not_9_out, not_15_out, not_16_out, not_19_out, not_20_out,
       not_22_out, not_25_out, not_26_out, not_27_out, not_32_out, not_36_out, not_37_out, PCE, ROE, RORW,
       RSTINS, s_r_ff_1_q, shift_register_1_q0, shift_register_1_q1, shift_register_1_q2,
       shift_register_2_q0, shift_register_2_q1, shift_register_2_q2, shift_register_3_q0,
       shift_register_3_q1, shift_register_3_q2, shift_register_4_q0, shift_register_4_q1,
       shift_register_4_q2, shift_register_5_q0, shift_register_5_q1, shift_register_5_q2,
       shift_register_5_q3, shift_register_5_q4, shift_register_6_q0, shift_register_6_q1,
       shift_register_6_q2, shift_register_7_q0, shift_register_7_q1, shift_register_7_q2,
       shift_register_7_q3, shift_register_7_q4, shift_register_7_q5, shift_register_7_q6,
       shift_register_8_q0, shift_register_8_q1, shift_register_8_q2, shift_register_8_q4,
       shift_register_8_q5, shift_register_8_q6, shift_register_8_q7, shift_register_9_q0,
       shift_register_9_q1, shift_register_9_q2, shift_register_10_q1, shift_register_10_q2,
       shift_register_10_q3, shift_register_10_q4, shift_register_10_q5, shift_register_11_q0,
       shift_register_11_q1, shift_register_11_q2, SHL, SLE, SRE, STORE, SUB, SUBE, TRE, TRRW;
  wire [3:0] L1, L1A_out, L1B_out, L2_out, L2_out_2, L3, not_28_out;
  wire [7:0] adder_1_out, alu_1_p14, alu_1_p15, and_1_out;
  wire [7:7] alu_1_p13;
  wire [30:0] Instrustion_Decoder_out_9;
  wire [31:12] Instrustion_Decoder_out_2;

  Pull_Resistor pull_resistor_1 (.node(out_8));
  assign out_7 = L1 | L3;  // OR_Gate or_1, 4 bits wide
  buf buffer_1 (DME, and_2_out);
  buf buffer_2 (L2E, and_6_out);
  buf buffer_3 (TRRW, and_6_out);
  Adder adder_1 (.a(out_3), .b(8'h1), .out(adder_1_out));  // open: cin, cout
  assign and_1_out = adder_1_out & {8{PCE}};  // AND_Gate and_1, 8 bits wide
  TempReg tempreg_1 (.CLK(CLK), .DO(out_6), .E(TRE), .DI(out_6), .RW(TRRW), .RS(out_7));
  Registor ACC (.E(ACCE), .CLK(CLK), .DO(out_8), .RW(ACCRW), .DI(out_8));
  assign out_8 = out_6 & {8{L4E}};  // AND_Gate L4, 8 bits wide
  Shift_Register #(.length(3)) shift_register_1 (
    .shift(STORE), .in(1'b1), .clk(CLK), .clr(RSTINS), .q0(shift_register_1_q0), .q1(shift_register_1_q1),
    .q2(shift_register_1_q2));  // open: out, load, d0, d1, d2
  not not_1 (not_1_out, shift_register_1_q1);
  and and_2 (and_2_out, shift_register_1_q0, not_1_out);
  not not_2 (DMRW, and_2_out);
  buf buffer_4 (L3E, and_2_out);
  buf buffer_5 (DMRW, and_3_out);
  buf buffer_6 (DME, and_3_out);
  buf buffer_7 (CRRW, and_4_out);
  buf buffer_8 (CRE, and_4_out);
  buf buffer_9 (LOE, and_5_out);
  buf buffer_10 (LORW, and_5_out);
  buf buffer_11 (ACCE, and_6_out);
  not not_3 (L1E, and_6_out);
  buf buffer_12 (TRE, and_6_out);
  buf buffer_13 (L4E, and_6_out);
  Register register_1 (.D(and_1_out), .en(PCE), .Q(out_3), .clk(CLK), .clr(PCRST));
  assign out_6 = {8{L8E}} & out_8;  // AND_Gate L8, 8 bits wide
  buf buffer_14 (INSEND, shift_register_1_q2);
  buf buffer_15 (TRRW, and_2_out);
  buf buffer_16 (TRE, and_2_out);
  Shift_Register #(.length(3)) shift_register_2 (
    .shift(LOAD_ADDRESS), .in(1'b1), .clk(CLK), .clr(RSTINS), .q0(shift_register_2_q0),
    .q1(shift_register_2_q1), .q2(shift_register_2_q2));  // open: out, load, d0, d1, d2
  not not_4 (not_4_out, shift_register_2_q1);
  and and_3 (and_3_out, shift_register_2_q0, not_4_out);
  buf buffer_17 (TRE, and_3_out);
  buf buffer_18 (L3E, and_3_out);
  Shift_Register #(.length(3)) shift_register_3 (
    .shift(LOAD_CARRY), .in(1'b1), .clk(CLK), .clr(RSTINS), .q0(shift_register_3_q0),
    .q1(shift_register_3_q1), .q2(shift_register_3_q2));  // open: out, load, d0, d1, d2
  not not_5 (not_5_out, shift_register_3_q1);
  and and_4 (and_4_out, shift_register_3_q0, not_5_out);
  buf buffer_19 (L3E, and_4_out);
  buf buffer_20 (TRE, and_4_out);
  Shift_Register #(.length(3)) shift_register_4 (
    .shift(LOAD_LO), .in(1'b1), .clk(CLK), .clr(RSTINS), .q0(shift_register_4_q0), .q1(shift_register_4_q1),
    .q2(shift_register_4_q2));  // open: out, load, d0, d1, d2
  buf buffer_21 (INSEND, shift_register_4_q2);
  not not_6 (not_6_out, shift_register_4_q1);
  and and_5 (and_5_out, shift_register_4_q0, not_6_out);
  buf buffer_22 (L3E, and_5_out);
  not not_7 (TRRW, and_5_out);
  buf buffer_23 (TRE, and_5_out);
  Shift_Register #(.length(5)) shift_register_5 (
    .shift(MOVE), .in(1'b1), .clk(CLK), .clr(RSTINS), .q0(shift_register_5_q0), .q1(shift_register_5_q1),
    .q2(shift_register_5_q2), .q3(shift_register_5_q3), .q4(shift_register_5_q4));  // open: out, load, d0, d1, d2, d3, d4
  not not_8 (not_8_out, shift_register_5_q1);
  not not_9 (not_9_out, shift_register_5_q3);
  and and_6 (and_6_out, shift_register_5_q0, not_8_out);
  and and_7 (and_7_out, shift_register_5_q2, not_9_out);
  not not_10 (ACCRW, and_6_out);
  buf buffer_24 (ACCE, and_7_out);
  Decoder Instrustion_Decoder (
    .in_1(out_5[19:12]),
    .out_2({Instrustion_Decoder_out_2, LOAD_CARRY, MOVE, LOAD_ADDRESS, LOAD_HI, MUL, LLS, LRS, SUB, ADD, STORE, LOAD_IMMEDIATE, LOAD_LO}),
    .out_9({EXIT, Instrustion_Decoder_out_9}));  // open: out_3, out_4, out_5, out_6, out_7, out_8
  Pull_Resistor pull_resistor_2 (.node(out_6));
  assign out_6 = {8{alu_1_p13[7]}} & {8{L6E}};  // AND_Gate L6, 8 bits wide
  buf buffer_25 (INSEND, shift_register_2_q2);
  not not_11 (TRRW, and_3_out);
  buf buffer_26 (INSEND, shift_register_3_q2);
  not not_12 (TRRW, and_4_out);
  buf buffer_27 (ACCE, and_8_out);
  buf buffer_28 (ACCE, and_10_out);
  buf buffer_29 (CRRW, and_9_out);
  buf buffer_30 (INSEND, shift_register_5_q4);
  not not_13 (TRRW, and_7_out);
  buf buffer_31 (TRE, and_7_out);
  buf buffer_32 (L3E, and_7_out);
  buf buffer_33 (L8E, and_7_out);
  assign out_6 = {8{L7E}} & out_4;  // AND_Gate L7, 8 bits wide
  // ALU alu_1: pin names not known; wires that end beside it: ADDE, SUBE, SHL, SLE, SRE, MULE, ALUC, ALUE, out_8, alu_1_p10, out_6, out_10, alu_1_p13[7], alu_1_p14, alu_1_p15
  buf buffer_34 (buffer_34_out, MUL);
  buf buffer_35 (buffer_34_out, SUB);
  buf buffer_36 (buffer_34_out, ADD);
  not not_14 (L1E, and_8_out);
  buf buffer_37 (L2E, and_8_out);
  buf buffer_38 (TRRW, and_8_out);
  buf buffer_39 (ACCRW, and_10_out);
  buf buffer_40 (L2E, and_10_out);
  Shift_Register #(.length(3)) shift_register_6 (
    .shift(LOAD_CARRY), .in(1'b1), .clk(CLK), .clr(RSTINS), .q0(shift_register_6_q0),
    .q1(shift_register_6_q1), .q2(shift_register_6_q2));  // open: out, load, d0, d1, d2
  buf buffer_41 (CRE, and_9_out);
  buf buffer_42 (L3E, and_9_out);
  buf buffer_43 (ACCRW, and_7_out);
  assign out_6 = {8{L5E}} & out_10;  // AND_Gate L5, 8 bits wide
  Registor CARRY (.E(CRE), .CLK(CLK), .DO({8{alu_1_p13[7]}}), .RW(CRRW), .DI({8{alu_1_p13[7]}}));
  Registor HI (.E(HIE), .CLK(CLK), .DO(alu_1_p15), .RW(HIRW));  // open: DI
  Pull_Resistor pull_resistor_3 (.node(buffer_34_out));
  Shift_Register #(.length(7)) shift_register_7 (
    .shift(buffer_34_out), .in(1'b1), .clk(CLK), .clr(RSTINS), .q0(shift_register_7_q0),
    .q1(shift_register_7_q1), .q2(shift_register_7_q2), .q3(shift_register_7_q3), .q4(shift_register_7_q4),
    .q5(shift_register_7_q5), .q6(shift_register_7_q6));  // open: out, load, d0, d1, d2, d3, d4, d5, d6
  not not_15 (not_15_out, shift_register_7_q1);
  and and_8 (and_8_out, shift_register_7_q0, not_15_out);
  buf buffer_44 (TRE, and_8_out);
  buf buffer_45 (L4E, and_8_out);
  buf buffer_46 (L1E, and_10_out);
  buf buffer_47 (TRE, and_10_out);
  buf buffer_48 (INSEND, shift_register_6_q2);
  not not_16 (not_16_out, shift_register_6_q1);
  and and_9 (and_9_out, shift_register_6_q0, not_16_out);
  buf buffer_49 (TRE, and_9_out);
  not not_17 (TRRW, and_9_out);
  buf buffer_50 (TRE, and_11_out);
  not not_18 (L1E, and_11_out);
  buf buffer_51 (ALUE, and_11_out);
  buf buffer_52 (TRRW, and_11_out);
  buf buffer_53 (TRRW, and_14_out);
  assign L3 = out_5[11:8] & {4{L3E}};  // AND_Gate L3, 4 bits wide
  Registor OR_2 (.E(ROE), .CLK(CLK), .DO(out_10), .RW(RORW), .DI(out_10));
  Registor LO (.E(LOE), .CLK(CLK), .DO(alu_1_p14), .RW(LORW));  // open: DI
  buf buffer_54 (INSEND, shift_register_7_q6);
  not not_19 (not_19_out, shift_register_7_q5);
  not not_20 (not_20_out, shift_register_7_q3);
  not not_21 (ACCRW, and_8_out);
  and and_10 (and_10_out, shift_register_7_q2, not_20_out);
  buf buffer_55 (TRRW, and_10_out);
  buf buffer_56 (CRE, and_10_out);
  buf buffer_57 (HIE, and_13_out);
  buf buffer_58 (HIRW, and_13_out);
  buf buffer_59 (buffer_59_out, LRS);
  Pull_Resistor pull_resistor_4 (.node(buffer_59_out));
  buf buffer_60 (buffer_59_out, LLS);
  Shift_Register shift_register_8 (
    .shift(buffer_59_out), .in(1'b1), .clk(CLK), .clr(RSTINS), .q0(shift_register_8_q0),
    .q1(shift_register_8_q1), .q2(shift_register_8_q2), .q4(shift_register_8_q4), .q5(shift_register_8_q5),
    .q6(shift_register_8_q6), .q7(shift_register_8_q7));  // open: out, load, d0, d1, d2, d3, q3, d4, d5, d6, d7
  not not_22 (not_22_out, shift_register_8_q1);
  buf buffer_61 (SHL, and_11_out);
  buf buffer_62 (L2E, and_11_out);
  and and_11 (and_11_out, shift_register_8_q0, not_22_out);
  not not_23 (RORW, and_14_out);
  buf buffer_63 (ROE, and_14_out);
  RAM ram_1 (.addr(out_4), .data(out_6), .sel(DME), .clk(CLK), .ld(DMRW));  // open: clr
  RAM #(.dataWidth(20)) ram_2 (.addr(out_3), .data({out_5[19:8], out_4}), .sel(IME), .clk(CLK), .ld(IME));  // open: clr
  Pull_Resistor pull_resistor_5 (.node(out_10));
  Pull_Resistor pull_resistor_6 (.node(PCE));
  Pull_Resistor pull_resistor_7 (.node(PCE));
  Pull_Resistor pull_resistor_8 (.node(INSEND));
  and and_12 (and_12_out, not_19_out, shift_register_7_q4);
  buf buffer_64 (L5E, and_12_out);
  buf buffer_65 (L3E, and_12_out);
  buf buffer_66 (TRE, and_12_out);
  not not_24 (CRRW, and_10_out);
  buf buffer_67 (ROE, and_10_out);
  Shift_Register #(.length(3)) shift_register_9 (
    .shift(LOAD_HI), .in(1'b1), .clk(CLK), .clr(RSTINS), .q0(shift_register_9_q0), .q1(shift_register_9_q1),
    .q2(shift_register_9_q2));  // open: out, load, d0, d1, d2
  not not_25 (not_25_out, shift_register_9_q1);
  and and_13 (and_13_out, shift_register_9_q0, not_25_out);
  buf buffer_68 (TRE, and_13_out);
  buf buffer_69 (L3E, and_13_out);
  not not_26 (not_26_out, shift_register_8_q4);
  not not_27 (not_27_out, shift_register_8_q6);
  and and_14 (and_14_out, shift_register_8_q2, not_26_out);
  and and_15 (and_15_out, and_14_out, LLS);
  and and_16 (and_16_out, and_14_out, LRS);
  buf buffer_70 (SLE, and_15_out);
  buf buffer_71 (SRE, and_16_out);
  Pull_Resistor pull_resistor_9 (.node({out_5[19:8], out_4}));
  Pull_Resistor pull_resistor_10 (.node(out_4));
  assign not_28_out = ~{4{L1E}};  // NOT_Gate not_28, 4 bits wide
  assign L1A_out = {4{L1E}} & L2_out;  // AND_Gate L1A, 4 bits wide
  assign L1 = L1A_out | L1B_out;  // OR_Gate or_3, 4 bits wide
  Pull_Resistor pull_resistor_11 (.node(ALUE));
  Pull_Resistor pull_resistor_12 (.node(ADDE));
  Pull_Resistor pull_resistor_13 (.node(SUBE));
  Pull_Resistor pull_resistor_14 (.node(SHL));
  Pull_Resistor pull_resistor_15 (.node(SLE));
  Pull_Resistor pull_resistor_16 (.node(SRE));
  Pull_Resistor pull_resistor_17 (.node(MULE));
  Pull_Resistor pull_resistor_18 (.node(ALUC));
  Pull_Resistor pull_resistor_19 (.node(HIE));
  Pull_Resistor pull_resistor_20 (.node(HIRW));
  Pull_Resistor pull_resistor_21 (.node(LOE));
  Pull_Resistor pull_resistor_22 (.node(LORW));
  S_R_Flip_Flop s_r_ff_1 (
    .S(INSEND), .clk(CLK), .R(shift_register_10_q4), .Q(s_r_ff_1_q), .en(not_36_out));  // open: Qn, preset, reset
  Shift_Register #(.length(6)) shift_register_10 (
    .shift(s_r_ff_1_q), .in(1'b1), .clk(CLK), .clr(shift_register_10_q5), .q0(RSTINS),
    .q1(shift_register_10_q1), .q2(shift_register_10_q2), .q3(shift_register_10_q3),
    .q4(shift_register_10_q4), .q5(shift_register_10_q5));  // open: out, load, d0, d1, d2, d3, d4, d5
  buf buffer_72 (RORW, and_12_out);
  buf buffer_73 (ROE, and_12_out);
  not not_29 (TRRW, and_12_out);
  buf buffer_74 (ALUE, and_10_out);
  not not_30 (RORW, and_10_out);
  buf buffer_75 (INSEND, shift_register_9_q2);
  not not_31 (TRRW, and_13_out);
  buf buffer_76 (INSEND, shift_register_8_q7);
  and and_17 (and_17_out, not_27_out, shift_register_8_q5);
  buf buffer_77 (L3E, and_17_out);
  buf buffer_78 (ALUE, and_14_out);
  buf buffer_79 (TRE, and_14_out);
  Clock u_CLK (.out(CLK));
  assign {L2_out, L2_out_2} = {8{L2E}} & out_4;  // AND_Gate L2, 8 bits wide
  assign L1B_out = L2_out_2 & not_28_out;  // AND_Gate L1B, 4 bits wide
  Pull_Resistor pull_resistor_23 (.node(L1E));
  Pull_Resistor pull_resistor_24 (.node(L2E));
  Pull_Resistor pull_resistor_25 (.node(L3E));
  Pull_Resistor pull_resistor_26 (.node(L4E));
  Pull_Resistor pull_resistor_27 (.node(L5E));
  Pull_Resistor pull_resistor_28 (.node(L6E));
  Pull_Resistor pull_resistor_29 (.node(L7E));
  Pull_Resistor pull_resistor_30 (.node(L8E));
  Pull_Resistor pull_resistor_31 (.node(IME));
  Pull_Resistor pull_resistor_32 (.node(IME));
  Pull_Resistor pull_resistor_33 (.node(DMRW));
  Pull_Resistor pull_resistor_34 (.node(DME));
  not not_32 (not_32_out, shift_register_10_q2);
  and and_18 (PCE, shift_register_10_q1, not_32_out);
  buf buffer_80 (LOE, and_10_out);
  not not_33 (HIRW, and_10_out);
  buf buffer_81 (HIE, and_10_out);
  not not_34 (LORW, and_10_out);
  Shift_Register #(.length(3)) shift_register_11 (
    .shift(LOAD_IMMEDIATE), .in(1'b1), .clk(CLK), .clr(RSTINS), .q0(shift_register_11_q0),
    .q1(shift_register_11_q1), .q2(shift_register_11_q2));  // open: out, load, d0, d1, d2
  buf buffer_82 (L7E, and_19_out);
  buf buffer_83 (L3E, and_19_out);
  buf buffer_84 (RORW, and_17_out);
  buf buffer_85 (L5E, and_17_out);
  not not_35 (TRRW, and_17_out);
  buf buffer_86 (TRE, and_17_out);
  not not_36 (not_36_out, shift_register_10_q5);
  nor nor_1 (nor_1_out, shift_register_10_q3, INSEND, IME);
  buf buffer_87 (INSEND, shift_register_11_q2);
  not not_37 (not_37_out, shift_register_11_q1);
  and and_19 (and_19_out, shift_register_11_q0, not_37_out);
  buf buffer_88 (TRE, and_19_out);
  not not_38 (TRRW, and_19_out);
  buf buffer_89 (ROE, and_17_out);
  Pull_Resistor pull_resistor_35 (.node(TRE));
  Pull_Resistor pull_resistor_36 (.node(TRRW));
  Pull_Resistor pull_resistor_37 (.node(CRRW));
  Pull_Resistor pull_resistor_38 (.node(CRE));
  Pull_Resistor pull_resistor_39 (.node(RORW));
  Pull_Resistor pull_resistor_40 (.node(ROE));
  Pull_Resistor pull_resistor_41 (.node(ACCRW));
  Pull_Resistor pull_resistor_42 (.node(ACCE));
  buf buffer_90 (ADDE, ADD);
  buf buffer_91 (SUBE, SUB);
  buf buffer_92 (MULE, MUL);
  S_R_Flip_Flop s_r_ff_2 (
    .S(shift_register_10_q3), .clk(CLK), .R(INSEND), .Q(IME), .preset(nor_1_out), .en(1'b1));  // open: Qn, reset

  assign out_5[7:0] = out_4;
  assign out_9 = out_6;
  // also tied to GND on the sheet: alu_1_p13[7]

  // Other names for the same wires on the sheet: PCIE = PCE; IMRW = IME; IMUX[7:0] = out_5[19:12]; TRS[3:0] = out_7

  // Notes on the sheet:
  //   buffer_1 drives only 1 and floats otherwise
  //   buffer_2 drives only 1 and floats otherwise
  //   buffer_3 drives only 1 and floats otherwise
  //   L4 drives only 1 and floats otherwise
  //   not_2 drives only 0 and floats otherwise
  //   buffer_4 drives only 1 and floats otherwise
  //   buffer_5 drives only 1 and floats otherwise
  //   buffer_6 drives only 1 and floats otherwise
  //   buffer_7 drives only 1 and floats otherwise
  //   buffer_8 drives only 1 and floats otherwise
  //   buffer_9 drives only 1 and floats otherwise
  //   buffer_10 drives only 1 and floats otherwise
  //   buffer_11 drives only 1 and floats otherwise
  //   not_3 drives only 0 and floats otherwise
  //   buffer_12 drives only 1 and floats otherwise
  //   buffer_13 drives only 1 and floats otherwise
  //   L8 drives only 1 and floats otherwise
  //   buffer_14 drives only 1 and floats otherwise
  //   buffer_15 drives only 1 and floats otherwise
  //   buffer_16 drives only 1 and floats otherwise
  //   buffer_17 drives only 1 and floats otherwise
  //   buffer_18 drives only 1 and floats otherwise
  //   buffer_19 drives only 1 and floats otherwise
  //   buffer_20 drives only 1 and floats otherwise
  //   buffer_21 drives only 1 and floats otherwise
  //   buffer_22 drives only 1 and floats otherwise
  //   not_7 drives only 0 and floats otherwise
  //   buffer_23 drives only 1 and floats otherwise
  //   not_10 drives only 0 and floats otherwise
  //   buffer_24 drives only 1 and floats otherwise
  //   L6 drives only 1 and floats otherwise
  //   buffer_25 drives only 1 and floats otherwise
  //   not_11 drives only 0 and floats otherwise
  //   buffer_26 drives only 1 and floats otherwise
  //   not_12 drives only 0 and floats otherwise
  //   buffer_27 drives only 1 and floats otherwise
  //   buffer_28 drives only 1 and floats otherwise
  //   buffer_29 drives only 1 and floats otherwise
  //   buffer_30 drives only 1 and floats otherwise
  //   not_13 drives only 0 and floats otherwise
  //   buffer_31 drives only 1 and floats otherwise
  //   buffer_32 drives only 1 and floats otherwise
  //   buffer_33 drives only 1 and floats otherwise
  //   L7 drives only 1 and floats otherwise
  //   buffer_34 drives only 1 and floats otherwise
  //   buffer_35 drives only 1 and floats otherwise
  //   buffer_36 drives only 1 and floats otherwise
  //   not_14 drives only 0 and floats otherwise
  //   buffer_37 drives only 1 and floats otherwise
  //   buffer_38 drives only 1 and floats otherwise
  //   buffer_39 drives only 1 and floats otherwise
  //   buffer_40 drives only 1 and floats otherwise
  //   buffer_41 drives only 1 and floats otherwise
  //   buffer_42 drives only 1 and floats otherwise
  //   buffer_43 drives only 1 and floats otherwise
  //   L5 drives only 1 and floats otherwise
  //   buffer_44 drives only 1 and floats otherwise
  //   buffer_45 drives only 1 and floats otherwise
  //   buffer_46 drives only 1 and floats otherwise
  //   buffer_47 drives only 1 and floats otherwise
  //   buffer_48 drives only 1 and floats otherwise
  //   buffer_49 drives only 1 and floats otherwise
  //   not_17 drives only 0 and floats otherwise
  //   buffer_50 drives only 1 and floats otherwise
  //   not_18 drives only 0 and floats otherwise
  //   buffer_51 drives only 1 and floats otherwise
  //   buffer_52 drives only 1 and floats otherwise
  //   buffer_53 drives only 1 and floats otherwise
  //   Data Memory
  //   Ins. Memory
  //   buffer_54 drives only 1 and floats otherwise
  //   not_21 drives only 0 and floats otherwise
  //   buffer_55 drives only 1 and floats otherwise
  //   buffer_56 drives only 1 and floats otherwise
  //   buffer_57 drives only 1 and floats otherwise
  //   buffer_58 drives only 1 and floats otherwise
  //   buffer_59 drives only 1 and floats otherwise
  //   buffer_60 drives only 1 and floats otherwise
  //   buffer_61 drives only 1 and floats otherwise
  //   buffer_62 drives only 1 and floats otherwise
  //   not_23 drives only 0 and floats otherwise
  //   buffer_63 drives only 1 and floats otherwise
  //   buffer_64 drives only 1 and floats otherwise
  //   buffer_65 drives only 1 and floats otherwise
  //   buffer_66 drives only 1 and floats otherwise
  //   not_24 drives only 0 and floats otherwise
  //   buffer_67 drives only 1 and floats otherwise
  //   buffer_68 drives only 1 and floats otherwise
  //   buffer_69 drives only 1 and floats otherwise
  //   buffer_70 drives only 1 and floats otherwise
  //   buffer_71 drives only 1 and floats otherwise
  //   buffer_72 drives only 1 and floats otherwise
  //   buffer_73 drives only 1 and floats otherwise
  //   not_29 drives only 0 and floats otherwise
  //   buffer_74 drives only 1 and floats otherwise
  //   not_30 drives only 0 and floats otherwise
  //   buffer_75 drives only 1 and floats otherwise
  //   not_31 drives only 0 and floats otherwise
  //   buffer_76 drives only 1 and floats otherwise
  //   buffer_77 drives only 1 and floats otherwise
  //   buffer_78 drives only 1 and floats otherwise
  //   buffer_79 drives only 1 and floats otherwise
  //   and_18 drives only 1 and floats otherwise
  //   buffer_80 drives only 1 and floats otherwise
  //   not_33 drives only 0 and floats otherwise
  //   buffer_81 drives only 1 and floats otherwise
  //   not_34 drives only 0 and floats otherwise
  //   buffer_82 drives only 1 and floats otherwise
  //   buffer_83 drives only 1 and floats otherwise
  //   buffer_84 drives only 1 and floats otherwise
  //   buffer_85 drives only 1 and floats otherwise
  //   not_35 drives only 0 and floats otherwise
  //   buffer_86 drives only 1 and floats otherwise
  //   buffer_87 drives only 1 and floats otherwise
  //   buffer_88 drives only 1 and floats otherwise
  //   not_38 drives only 0 and floats otherwise
  //   buffer_89 drives only 1 and floats otherwise
  //   buffer_90 drives only 1 and floats otherwise
  //   buffer_91 drives only 1 and floats otherwise
  //   buffer_92 drives only 1 and floats otherwise
endmodule

module ALU (
  input  C,
  input  [7:0] In1,
  input  [7:0] In2,
  input  E,
  input  [7:0] Carry_In,
  input  [2:0] Shift_Amount,
  input  Add,
  input  Sub,
  input  SL,
  input  SR,
  input  Mul,
  input  S6,
  input  Clear,
  output Carry,
  output [7:0] Out,
  output [7:0] HI,
  output [7:0] LO
);

  wire [2:0] priority_encoder_1_out;
  wire [7:0] adder_1_out, shifter_1_out, shifter_2_out, subtractor_1_out;

  Multiplier multiplier_1 (.a(In1), .b(In2), .out(LO), .cin(Carry_In), .cout(HI));
  Adder adder_1 (.a(In2), .b(In1), .out(adder_1_out), .cin(C), .cout(Carry));
  Pull_Resistor pull_resistor_1 (.node(In1));
  Pull_Resistor pull_resistor_2 (.node(In2));
  Subtractor subtractor_1 (.a(In1), .b(In2), .out(subtractor_1_out), .bin(C), .bout(Carry));
  Shifter shifter_1 (.in(In1), .\dist (Shift_Amount), .out(shifter_1_out));
  Shifter #(.shift("lr")) shifter_2 (.in(In1), .\dist (Shift_Amount), .out(shifter_2_out));
  Multiplexer #(.select(3), .width(8)) multiplexer_1 (
    .in0(adder_1_out), .in1(subtractor_1_out), .in3(shifter_1_out), .in4(shifter_2_out), .in5(LO),
    .in7({8{1'b0}}), .out(Out), .sel(priority_encoder_1_out), .en(E));  // open: in2, in6
  Priority_Encoder #(.disabled(0)) priority_encoder_1 (
    .in0(Add), .in1(Sub), .in3(SL), .in4(SR), .in5(Mul), .in6(S6), .in7(Clear), .out(priority_encoder_1_out));  // open: in2, en_in
endmodule

// RegistorBank
module TempReg (
  input  E,
  input  [3:0] RS,
  input  [7:0] DI,
  input  CLK,
  input  RW,
  output [7:0] DO
);

  wire and_1_out, demultiplexer_1_out0, demultiplexer_1_out1, demultiplexer_1_out2, demultiplexer_1_out3,
       demultiplexer_1_out4, demultiplexer_1_out5, demultiplexer_1_out6, demultiplexer_1_out7,
       demultiplexer_1_out8, demultiplexer_1_out9, demultiplexer_1_out10, demultiplexer_1_out11,
       demultiplexer_1_out12, demultiplexer_1_out13, demultiplexer_1_out14, demultiplexer_1_out15, not_2_out;
  wire [7:0] and_2_out, multiplexer_1_out, not_1_out, register_1_q, register_2_q, register_3_q, register_4_q,
       register_5_q, register_6_q, register_7_q, register_8_q, register_9_q, register_10_q, register_11_q,
       register_12_q, register_13_q, register_14_q, register_15_q, register_16_q;

  Demultiplexer #(.select(4), .disabled(0)) demultiplexer_1 (
    .out0(demultiplexer_1_out0), .out1(demultiplexer_1_out1), .out2(demultiplexer_1_out2),
    .out3(demultiplexer_1_out3), .out4(demultiplexer_1_out4), .out5(demultiplexer_1_out5),
    .out6(demultiplexer_1_out6), .out7(demultiplexer_1_out7), .out8(demultiplexer_1_out8),
    .out9(demultiplexer_1_out9), .out10(demultiplexer_1_out10), .out11(demultiplexer_1_out11),
    .out12(demultiplexer_1_out12), .out13(demultiplexer_1_out13), .out14(demultiplexer_1_out14),
    .out15(demultiplexer_1_out15), .sel(RS), .en(E));  // open: in
  and and_1 (and_1_out, CLK, not_2_out);
  assign and_2_out = DI & not_1_out;  // AND_Gate and_2, 8 bits wide
  assign not_1_out = ~{8{RW}};  // NOT_Gate not_1, 8 bits wide
  not not_2 (not_2_out, RW);
  Register register_1 (.D(and_2_out), .en(demultiplexer_1_out0), .Q(register_1_q), .clk(and_1_out), .clr(1'b0));
  Register register_2 (.D(and_2_out), .en(demultiplexer_1_out1), .Q(register_2_q), .clk(and_1_out), .clr(1'b0));
  Register register_3 (.D(and_2_out), .en(demultiplexer_1_out2), .Q(register_3_q), .clk(and_1_out), .clr(1'b0));
  Register register_4 (.D(and_2_out), .en(demultiplexer_1_out3), .Q(register_4_q), .clk(and_1_out), .clr(1'b0));
  Register register_5 (.D(and_2_out), .en(demultiplexer_1_out4), .Q(register_5_q), .clk(and_1_out), .clr(1'b0));
  Register register_6 (.D(and_2_out), .en(demultiplexer_1_out5), .Q(register_6_q), .clk(and_1_out), .clr(1'b0));
  Register register_7 (.D(and_2_out), .en(demultiplexer_1_out6), .Q(register_7_q), .clk(and_1_out), .clr(1'b0));
  Register register_8 (.D(and_2_out), .en(demultiplexer_1_out7), .Q(register_8_q), .clk(and_1_out), .clr(1'b0));
  Register register_9 (.D(and_2_out), .en(demultiplexer_1_out8), .Q(register_9_q), .clk(and_1_out), .clr(1'b0));
  Register register_10 (.D(and_2_out), .en(demultiplexer_1_out9), .Q(register_10_q), .clk(and_1_out), .clr(1'b0));
  Register register_11 (.D(and_2_out), .en(demultiplexer_1_out10), .Q(register_11_q), .clk(and_1_out), .clr(1'b0));
  Register register_12 (.D(and_2_out), .en(demultiplexer_1_out11), .Q(register_12_q), .clk(and_1_out), .clr(1'b0));
  Register register_13 (.D(and_2_out), .en(demultiplexer_1_out12), .Q(register_13_q), .clk(and_1_out), .clr(1'b0));
  Register register_14 (.D(and_2_out), .en(demultiplexer_1_out13), .Q(register_14_q), .clk(and_1_out), .clr(1'b0));
  Register register_15 (.D(and_2_out), .en(demultiplexer_1_out14), .Q(register_15_q), .clk(and_1_out), .clr(1'b0));
  Register register_16 (.D(and_2_out), .en(demultiplexer_1_out15), .Q(register_16_q), .clk(and_1_out), .clr(1'b0));
  assign DO = multiplexer_1_out & {8{RW}};  // AND_Gate and_3, 8 bits wide
  Multiplexer #(.select(4), .width(8)) multiplexer_1 (
    .in0(register_1_q), .in1(register_2_q), .in2(register_3_q), .in3(register_4_q), .in4(register_5_q),
    .in5(register_6_q), .in6(register_7_q), .in7(register_8_q), .in8(register_9_q), .in9(register_10_q),
    .in10(register_11_q), .in11(register_12_q), .in12(register_13_q), .in13(register_14_q),
    .in14(register_15_q), .in15(register_16_q), .out(multiplexer_1_out), .sel(RS), .en(E));

  // Notes on the sheet:
  //   DI: pull=down
  //   DO: pull=down
  //   and_3 drives only 1 and floats otherwise
endmodule

module Registor (
  input  E,
  input  [7:0] DI,
  input  CLK,
  input  RW,
  output [7:0] DO
);

  wire and_1_out, not_2_out;
  wire [7:0] and_2_out, not_1_out, Reg_q;

  and and_1 (and_1_out, CLK, not_2_out);
  assign and_2_out = DI & not_1_out;  // AND_Gate and_2, 8 bits wide
  Register Reg (.D(and_2_out), .en(E), .Q(Reg_q), .clk(and_1_out));  // open: clr
  assign not_1_out = ~{8{RW}};  // NOT_Gate not_1, 8 bits wide
  not not_2 (not_2_out, RW);
  assign DO = Reg_q & {8{RW}};  // AND_Gate and_3, 8 bits wide

  // Notes on the sheet:
  //   CLK: pull=down
  //   and_3 drives only 1 and floats otherwise
endmodule

module Registor_1bit (
  input  E,
  input  RW,
  input  CLK,
  output Data
);

  wire Reg_q, undriven;

  Register #(.width(1)) Reg (.D(undriven), .en(E), .Q(Reg_q), .clk(CLK));  // open: clr
  Multiplexer multiplexer_1 (.in0(undriven), .in1(Reg_q), .out(Data), .en(RW));  // open: sel
endmodule

module Decoder (
  input  [7:0] in_1,
  output [31:0] out_2,
  output [31:0] out_3,
  output [31:0] out_4,
  output [31:0] out_5,
  output [31:0] out_6,
  output [31:0] out_7,
  output [31:0] out_8,
  output [31:0] out_9
);

  wire decoder_1_out0, decoder_1_out1, decoder_1_out2, decoder_1_out3, decoder_1_out4, decoder_1_out5,
       decoder_1_out6, decoder_1_out7;

  Decoder_part #(.select(3)) decoder_1 (
    .out0(decoder_1_out0), .out1(decoder_1_out1), .out2(decoder_1_out2), .out3(decoder_1_out3),
    .out4(decoder_1_out4), .out5(decoder_1_out5), .out6(decoder_1_out6), .out7(decoder_1_out7),
    .sel(in_1[7:5]));  // open: en
  Decoder_part #(.select(5), .disabled(0)) decoder_2 (
    .out0(out_2[0]), .out1(out_2[1]), .out2(out_2[2]), .out3(out_2[3]), .out4(out_2[4]), .out5(out_2[5]),
    .out6(out_2[6]), .out7(out_2[7]), .out8(out_2[8]), .out9(out_2[9]), .out10(out_2[10]), .out11(out_2[11]),
    .out12(out_2[12]), .out13(out_2[13]), .out14(out_2[14]), .out15(out_2[15]), .out16(out_2[16]),
    .out17(out_2[17]), .out18(out_2[18]), .out19(out_2[19]), .out20(out_2[20]), .out21(out_2[21]),
    .out22(out_2[22]), .out23(out_2[23]), .out24(out_2[24]), .out25(out_2[25]), .out26(out_2[26]),
    .out27(out_2[27]), .out28(out_2[28]), .out29(out_2[29]), .out30(out_2[30]), .out31(out_2[31]),
    .sel(in_1[4:0]), .en(decoder_1_out0));
  Decoder_part #(.select(5), .disabled(0)) decoder_3 (
    .out0(out_3[0]), .out1(out_3[1]), .out2(out_3[2]), .out3(out_3[3]), .out4(out_3[4]), .out5(out_3[5]),
    .out6(out_3[6]), .out7(out_3[7]), .out8(out_3[8]), .out9(out_3[9]), .out10(out_3[10]), .out11(out_3[11]),
    .out12(out_3[12]), .out13(out_3[13]), .out14(out_3[14]), .out15(out_3[15]), .out16(out_3[16]),
    .out17(out_3[17]), .out18(out_3[18]), .out19(out_3[19]), .out20(out_3[20]), .out21(out_3[21]),
    .out22(out_3[22]), .out23(out_3[23]), .out24(out_3[24]), .out25(out_3[25]), .out26(out_3[26]),
    .out27(out_3[27]), .out28(out_3[28]), .out29(out_3[29]), .out30(out_3[30]), .out31(out_3[31]),
    .sel(in_1[4:0]), .en(decoder_1_out1));
  Decoder_part #(.select(5), .disabled(0)) decoder_4 (
    .out0(out_4[0]), .out1(out_4[1]), .out2(out_4[2]), .out3(out_4[3]), .out4(out_4[4]), .out5(out_4[5]),
    .out6(out_4[6]), .out7(out_4[7]), .out8(out_4[8]), .out9(out_4[9]), .out10(out_4[10]), .out11(out_4[11]),
    .out12(out_4[12]), .out13(out_4[13]), .out14(out_4[14]), .out15(out_4[15]), .out16(out_4[16]),
    .out17(out_4[17]), .out18(out_4[18]), .out19(out_4[19]), .out20(out_4[20]), .out21(out_4[21]),
    .out22(out_4[22]), .out23(out_4[23]), .out24(out_4[24]), .out25(out_4[25]), .out26(out_4[26]),
    .out27(out_4[27]), .out28(out_4[28]), .out29(out_4[29]), .out30(out_4[30]), .out31(out_4[31]),
    .sel(in_1[4:0]), .en(decoder_1_out2));
  Decoder_part #(.select(5), .disabled(0)) decoder_5 (
    .out0(out_5[0]), .out1(out_5[1]), .out2(out_5[2]), .out3(out_5[3]), .out4(out_5[4]), .out5(out_5[5]),
    .out6(out_5[6]), .out7(out_5[7]), .out8(out_5[8]), .out9(out_5[9]), .out10(out_5[10]), .out11(out_5[11]),
    .out12(out_5[12]), .out13(out_5[13]), .out14(out_5[14]), .out15(out_5[15]), .out16(out_5[16]),
    .out17(out_5[17]), .out18(out_5[18]), .out19(out_5[19]), .out20(out_5[20]), .out21(out_5[21]),
    .out22(out_5[22]), .out23(out_5[23]), .out24(out_5[24]), .out25(out_5[25]), .out26(out_5[26]),
    .out27(out_5[27]), .out28(out_5[28]), .out29(out_5[29]), .out30(out_5[30]), .out31(out_5[31]),
    .sel(in_1[4:0]), .en(decoder_1_out3));
  Decoder_part #(.select(5), .disabled(0)) decoder_6 (
    .out0(out_6[0]), .out1(out_6[1]), .out2(out_6[2]), .out3(out_6[3]), .out4(out_6[4]), .out5(out_6[5]),
    .out6(out_6[6]), .out7(out_6[7]), .out8(out_6[8]), .out9(out_6[9]), .out10(out_6[10]), .out11(out_6[11]),
    .out12(out_6[12]), .out13(out_6[13]), .out14(out_6[14]), .out15(out_6[15]), .out16(out_6[16]),
    .out17(out_6[17]), .out18(out_6[18]), .out19(out_6[19]), .out20(out_6[20]), .out21(out_6[21]),
    .out22(out_6[22]), .out23(out_6[23]), .out24(out_6[24]), .out25(out_6[25]), .out26(out_6[26]),
    .out27(out_6[27]), .out28(out_6[28]), .out29(out_6[29]), .out30(out_6[30]), .out31(out_6[31]),
    .sel(in_1[4:0]), .en(decoder_1_out4));
  Decoder_part #(.select(5), .disabled(0)) decoder_7 (
    .out0(out_7[0]), .out1(out_7[1]), .out2(out_7[2]), .out3(out_7[3]), .out4(out_7[4]), .out5(out_7[5]),
    .out6(out_7[6]), .out7(out_7[7]), .out8(out_7[8]), .out9(out_7[9]), .out10(out_7[10]), .out11(out_7[11]),
    .out12(out_7[12]), .out13(out_7[13]), .out14(out_7[14]), .out15(out_7[15]), .out16(out_7[16]),
    .out17(out_7[17]), .out18(out_7[18]), .out19(out_7[19]), .out20(out_7[20]), .out21(out_7[21]),
    .out22(out_7[22]), .out23(out_7[23]), .out24(out_7[24]), .out25(out_7[25]), .out26(out_7[26]),
    .out27(out_7[27]), .out28(out_7[28]), .out29(out_7[29]), .out30(out_7[30]), .out31(out_7[31]),
    .sel(in_1[4:0]), .en(decoder_1_out5));
  Decoder_part #(.select(5), .disabled(0)) decoder_8 (
    .out0(out_8[0]), .out1(out_8[1]), .out2(out_8[2]), .out3(out_8[3]), .out4(out_8[4]), .out5(out_8[5]),
    .out6(out_8[6]), .out7(out_8[7]), .out8(out_8[8]), .out9(out_8[9]), .out10(out_8[10]), .out11(out_8[11]),
    .out12(out_8[12]), .out13(out_8[13]), .out14(out_8[14]), .out15(out_8[15]), .out16(out_8[16]),
    .out17(out_8[17]), .out18(out_8[18]), .out19(out_8[19]), .out20(out_8[20]), .out21(out_8[21]),
    .out22(out_8[22]), .out23(out_8[23]), .out24(out_8[24]), .out25(out_8[25]), .out26(out_8[26]),
    .out27(out_8[27]), .out28(out_8[28]), .out29(out_8[29]), .out30(out_8[30]), .out31(out_8[31]),
    .sel(in_1[4:0]), .en(decoder_1_out6));
  Decoder_part #(.select(5), .disabled(0)) decoder_9 (
    .out0(out_9[0]), .out1(out_9[1]), .out2(out_9[2]), .out3(out_9[3]), .out4(out_9[4]), .out5(out_9[5]),
    .out6(out_9[6]), .out7(out_9[7]), .out8(out_9[8]), .out9(out_9[9]), .out10(out_9[10]), .out11(out_9[11]),
    .out12(out_9[12]), .out13(out_9[13]), .out14(out_9[14]), .out15(out_9[15]), .out16(out_9[16]),
    .out17(out_9[17]), .out18(out_9[18]), .out19(out_9[19]), .out20(out_9[20]), .out21(out_9[21]),
    .out22(out_9[22]), .out23(out_9[23]), .out24(out_9[24]), .out25(out_9[25]), .out26(out_9[26]),
    .out27(out_9[27]), .out28(out_9[28]), .out29(out_9[29]), .out30(out_9[30]), .out31(out_9[31]),
    .sel(in_1[4:0]), .en(decoder_1_out7));
endmodule
