// Logisim project FULL_SUB (1).circ as structural Verilog: 2 circuits, main circuit main
module main (
  input  [3:0] A,
  input  [3:0] B,
  input  Cin,
  output [3:0] out,
  output carryout
);

  wire and_1_out, and_2_out, and_3_out, and_4_out, and_5_out, and_6_out, and_7_out, and_8_out, or_1_out,
       or_2_out, or_3_out, xor_1_out, xor_2_out, xor_4_out, xor_5_out, xor_7_out, xor_8_out, xor_10_out,
       xor_11_out;

  xor xor_1 (xor_1_out, Cin, B[0]);
  xor xor_2 (xor_2_out, xor_1_out, A[0]);
  and and_1 (and_1_out, A[0], xor_1_out);
  xor xor_3 (out[0], xor_2_out, Cin);
  and and_2 (and_2_out, Cin, xor_2_out);
  or or_1 (or_1_out, and_2_out, and_1_out);
  xor xor_4 (xor_4_out, Cin, B[1]);
  xor xor_5 (xor_5_out, xor_4_out, A[1]);
  and and_3 (and_3_out, A[1], xor_4_out);
  xor xor_6 (out[1], xor_5_out, or_1_out);
  and and_4 (and_4_out, or_1_out, xor_5_out);
  or or_2 (or_2_out, and_4_out, and_3_out);
  xor xor_7 (xor_7_out, Cin, B[2]);
  xor xor_8 (xor_8_out, xor_7_out, A[2]);
  xor xor_9 (out[2], xor_8_out, or_2_out);
  and and_5 (and_5_out, or_2_out, xor_8_out);
  and and_6 (and_6_out, A[2], xor_7_out);
  or or_3 (or_3_out, and_5_out, and_6_out);
  xor xor_10 (xor_10_out, Cin, B[3]);
  xor xor_11 (xor_11_out, xor_10_out, A[3]);
  and and_7 (and_7_out, A[3], xor_10_out);
  xor xor_12 (out[3], xor_11_out, or_3_out);
  and and_8 (and_8_out, or_3_out, xor_11_out);
  or or_4 (carryout, and_8_out, and_7_out);

  // Notes on the sheet:
  //   B: pull=down
  //   A: pull=down
  //   Cin: pull=down
endmodule

module _8_bit_Subtractor (
);

  wire [7:0] undriven, undriven_2;

  Subtractor subtractor_1 (.a(undriven), .b(undriven_2));  // open: out, bin, bout
endmodule
